// Digital circuit 4_Bit_Multiplexer Example.dig as structural Verilog
module _4_Bit_Multiplexer_Example (
  input  s_0,
  input  s_1,
  input  a_0,
  input  a_1,
  input  a_2,
  input  a_3,
  output saida
);

  wire and_1_out, and_2_out, and_3_out, and_4_out, and_5_out, and_6_out, and_7_out, and_8_out, not_1_out,
       not_2_out, not_3_out, not_4_out;

  not not_1 (not_1_out, s_1);
  not not_2 (not_2_out, s_0);
  not not_3 (not_3_out, s_1);
  not not_4 (not_4_out, s_0);
  and and_1 (and_1_out, not_1_out, not_2_out);
  and and_2 (and_2_out, not_3_out, s_0);
  and and_3 (and_3_out, s_1, not_4_out);
  and and_4 (and_4_out, s_1, s_0);
  and and_5 (and_5_out, a_0, and_1_out);
  and and_6 (and_6_out, a_1, and_2_out);
  and and_7 (and_7_out, a_2, and_3_out);
  and and_8 (and_8_out, a_3, and_4_out);
  or or_1 (saida, and_5_out, and_6_out, and_7_out, and_8_out);
endmodule
