// Digital circuit 4_Bit_Multiplier Example.dig as structural Verilog
module _4_Bit_Multiplier_Example (
  input  in_1,
  input  in_2,
  input  in_3,
  input  in_4,
  input  in_5,
  input  in_6,
  input  in_7,
  input  in_8,
  output out_9,
  output out_10,
  output out_11,
  output out_12,
  output out_13,
  output out_14,
  output out_15,
  output out_16
);

  wire [3:0] and_2_out, and_3_out, and_4_out;
  wire [3:1] _4_bit_sum_1_p4, _4_bit_sum_2_p4, and_1_out;
  wire [3:3] _4_bit_sum_1_p5, _4_bit_sum_2_p5;

  assign {and_1_out, out_9} = {in_4, in_3, in_2, in_1} & {4{in_5}};  // And and_1, 4 bits wide
  assign and_2_out = {in_4, in_3, in_2, in_1} & {4{in_6}};  // And and_2, 4 bits wide
  assign and_3_out = {in_4, in_3, in_2, in_1} & {4{in_7}};  // And and_3, 4 bits wide
  assign and_4_out = {in_4, in_3, in_2, in_1} & {4{in_8}};  // And and_4, 4 bits wide
  // _4_Bit_Sum _4_bit_sum_1: pin names not known; wires that end beside it: {1'b0, and_1_out}, and_2_out, 1'b0, {_4_bit_sum_1_p4, out_10}, _4_bit_sum_1_p5[3]
  // _4_Bit_Sum _4_bit_sum_2: pin names not known; wires that end beside it: {_4_bit_sum_1_p5[3], _4_bit_sum_1_p4}, and_3_out, 1'b0, {_4_bit_sum_2_p4, out_11}, _4_bit_sum_2_p5[3]
  // _4_Bit_Sum _4_bit_sum_3: pin names not known; wires that end beside it: {_4_bit_sum_2_p5[3], _4_bit_sum_2_p4}, and_4_out, 1'b0, {out_15, out_14, out_13, out_12}, out_16
endmodule
