// Digital circuit EEPROM Example.dig as structural Verilog
module EEPROM_Example (
  input  D_in0,
  input  CLK,
  input  EN,
  input  D_in1,
  input  D_in2,
  input  D_in3,
  input  A_0,
  input  A_1,
  input  A_2,
  input  A_3,
  input  WE,
  output D_out0,
  output D_out1,
  output D_out2,
  output D_out3
);

  EEPROM #(.AddrBits(4), .Bits(4)) eeprom_1 (
    .A({A_3, A_2, A_1, A_0}), .CS(EN), .WE(WE), .OE(CLK), .D({D_out3, D_out2, D_out1, D_out0}));
  assign {D_out3, D_out2, D_out1, D_out0} = WE ? {D_in3, D_in2, D_in1, D_in0} : 4'bz;  // Driver driver_1

  // Notes on the sheet:
  //   contents of eeprom_1 (hex, n*v repeats v):
  //   a,d,f,3,4,5,6,7
endmodule
