// Digital circuit Latch_SR Example.dig as structural Verilog
module Latch_SR_Example (
  input  S,
  input  R,
  output Q
);

  wire nand_2_out;

  nand nand_1 (Q, S, nand_2_out);
  nand nand_2 (nand_2_out, Q, R);
endmodule
