// Digital circuit Sinchronous_Counter Example D.dig as structural Verilog
module Sinchronous_Counter_Example_D (
  input  clk
);

  wire and_1_out, and_2_out, and_3_out, and_4_out, and_5_out, and_6_out, and_7_out, and_8_out, and_9_out,
       and_10_out, and_11_out, and_12_out, and_13_out, and_14_out, and_15_out, and_16_out, and_17_out,
       and_18_out, and_19_out, and_20_out, and_21_out, and_22_out, and_23_out, and_24_out, and_25_out,
       and_26_out, and_27_out, and_28_out, and_29_out, and_30_out, and_31_out, and_32_out, and_33_out,
       and_34_out, and_35_out, and_36_out, and_37_out, and_38_out, d_ff_1_q, d_ff_2_q, d_ff_3_q, d_ff_4_q,
       d_ff_5_q, d_ff_6_q, d_ff_7_q, d_ff_8_q, d_ff_9_q, d_ff_10_q, d_ff_11_q, d_ff_12_q, d_ff_13_q,
       d_ff_14_q, not_1_out, not_2_out, not_3_out, not_4_out, not_5_out, not_6_out, not_7_out, not_8_out,
       not_9_out, not_10_out, not_11_out, not_12_out, not_13_out, not_14_out, not_15_out, not_16_out,
       not_17_out, not_18_out, not_19_out, not_20_out, not_21_out, not_22_out, not_23_out, not_24_out,
       not_25_out, not_26_out, not_27_out, or_1_out, or_2_out, or_3_out, or_4_out, or_5_out, or_6_out,
       or_7_out, or_8_out, or_9_out, or_10_out, or_11_out, or_12_out, or_13_out;

  D_FF d_ff_1 (.D(not_1_out), .C(clk), .Q(d_ff_1_q));  // open: nQ
  not not_1 (not_1_out, d_ff_1_q);
  LED led_1 (.in(d_ff_1_q));
  or or_1 (or_1_out, and_2_out, and_1_out);
  D_FF d_ff_2 (.D(or_1_out), .C(clk), .Q(d_ff_2_q));  // open: nQ
  and and_1 (and_1_out, not_2_out, d_ff_1_q);
  and and_2 (and_2_out, d_ff_2_q, not_3_out);
  LED led_2 (.in(d_ff_2_q));
  not not_2 (not_2_out, d_ff_2_q);
  not not_3 (not_3_out, d_ff_1_q);
  and and_3 (and_3_out, d_ff_2_q, d_ff_1_q);
  or or_2 (or_2_out, and_5_out, and_4_out);
  and and_4 (and_4_out, not_4_out, and_3_out);
  and and_5 (and_5_out, d_ff_3_q, not_5_out);
  D_FF d_ff_3 (.D(or_2_out), .C(clk), .Q(d_ff_3_q));  // open: nQ
  not not_4 (not_4_out, d_ff_3_q);
  not not_5 (not_5_out, and_3_out);
  LED led_3 (.in(d_ff_3_q));
  and and_6 (and_6_out, d_ff_3_q, and_3_out);
  or or_3 (or_3_out, and_8_out, and_7_out);
  D_FF d_ff_4 (.D(or_3_out), .C(clk), .Q(d_ff_4_q));  // open: nQ
  and and_7 (and_7_out, not_6_out, and_6_out);
  not not_6 (not_6_out, d_ff_4_q);
  not not_7 (not_7_out, and_6_out);
  and and_8 (and_8_out, d_ff_4_q, not_7_out);
  LED led_4 (.in(d_ff_4_q));
  and and_9 (and_9_out, d_ff_4_q, and_6_out);
  or or_4 (or_4_out, and_11_out, and_10_out);
  D_FF d_ff_5 (.D(or_4_out), .C(clk), .Q(d_ff_5_q));  // open: nQ
  and and_10 (and_10_out, not_8_out, and_9_out);
  and and_11 (and_11_out, d_ff_5_q, not_9_out);
  LED led_5 (.in(d_ff_5_q));
  and and_12 (and_12_out, d_ff_5_q, and_9_out);
  not not_8 (not_8_out, d_ff_5_q);
  not not_9 (not_9_out, and_9_out);
  or or_5 (or_5_out, and_14_out, and_13_out);
  D_FF d_ff_6 (.D(or_5_out), .C(clk), .Q(d_ff_6_q));  // open: nQ
  and and_13 (and_13_out, not_10_out, and_12_out);
  and and_14 (and_14_out, d_ff_6_q, not_11_out);
  LED led_6 (.in(d_ff_6_q));
  not not_10 (not_10_out, d_ff_6_q);
  not not_11 (not_11_out, and_12_out);
  and and_15 (and_15_out, d_ff_6_q, and_12_out);
  or or_6 (or_6_out, and_17_out, and_16_out);
  and and_16 (and_16_out, not_12_out, and_15_out);
  and and_17 (and_17_out, d_ff_7_q, not_13_out);
  D_FF d_ff_7 (.D(or_6_out), .C(clk), .Q(d_ff_7_q));  // open: nQ
  not not_12 (not_12_out, d_ff_7_q);
  not not_13 (not_13_out, and_15_out);
  LED led_7 (.in(d_ff_7_q));
  and and_18 (and_18_out, d_ff_7_q, and_15_out);
  or or_7 (or_7_out, and_20_out, and_19_out);
  D_FF d_ff_8 (.D(or_7_out), .C(clk), .Q(d_ff_8_q));  // open: nQ
  and and_19 (and_19_out, not_14_out, and_18_out);
  not not_14 (not_14_out, d_ff_8_q);
  not not_15 (not_15_out, and_18_out);
  and and_20 (and_20_out, d_ff_8_q, not_15_out);
  LED led_8 (.in(d_ff_8_q));
  and and_21 (and_21_out, d_ff_8_q, and_18_out);
  or or_8 (or_8_out, and_23_out, and_22_out);
  D_FF d_ff_9 (.D(or_8_out), .C(clk), .Q(d_ff_9_q));  // open: nQ
  and and_22 (and_22_out, not_16_out, and_21_out);
  and and_23 (and_23_out, d_ff_9_q, not_17_out);
  LED led_9 (.in(d_ff_9_q));
  and and_24 (and_24_out, d_ff_9_q, and_21_out);
  not not_16 (not_16_out, d_ff_9_q);
  not not_17 (not_17_out, and_21_out);
  or or_9 (or_9_out, and_26_out, and_25_out);
  D_FF d_ff_10 (.D(or_9_out), .C(clk), .Q(d_ff_10_q));  // open: nQ
  and and_25 (and_25_out, not_18_out, and_24_out);
  and and_26 (and_26_out, d_ff_10_q, not_19_out);
  LED led_10 (.in(d_ff_10_q));
  not not_18 (not_18_out, d_ff_10_q);
  not not_19 (not_19_out, and_24_out);
  and and_27 (and_27_out, d_ff_10_q, and_24_out);
  or or_10 (or_10_out, and_29_out, and_28_out);
  and and_28 (and_28_out, not_20_out, and_27_out);
  and and_29 (and_29_out, d_ff_11_q, not_21_out);
  D_FF d_ff_11 (.D(or_10_out), .C(clk), .Q(d_ff_11_q));  // open: nQ
  not not_20 (not_20_out, d_ff_11_q);
  not not_21 (not_21_out, and_27_out);
  LED led_11 (.in(d_ff_11_q));
  and and_30 (and_30_out, d_ff_11_q, and_27_out);
  or or_11 (or_11_out, and_32_out, and_31_out);
  D_FF d_ff_12 (.D(or_11_out), .C(clk), .Q(d_ff_12_q));  // open: nQ
  and and_31 (and_31_out, not_22_out, and_30_out);
  not not_22 (not_22_out, d_ff_12_q);
  not not_23 (not_23_out, and_30_out);
  and and_32 (and_32_out, d_ff_12_q, not_23_out);
  LED led_12 (.in(d_ff_12_q));
  and and_33 (and_33_out, d_ff_12_q, and_30_out);
  or or_12 (or_12_out, and_35_out, and_34_out);
  D_FF d_ff_13 (.D(or_12_out), .C(clk), .Q(d_ff_13_q));  // open: nQ
  and and_34 (and_34_out, not_24_out, and_33_out);
  and and_35 (and_35_out, d_ff_13_q, not_25_out);
  LED led_13 (.in(d_ff_13_q));
  and and_36 (and_36_out, d_ff_13_q, and_33_out);
  not not_24 (not_24_out, d_ff_13_q);
  not not_25 (not_25_out, and_33_out);
  or or_13 (or_13_out, and_38_out, and_37_out);
  D_FF d_ff_14 (.D(or_13_out), .C(clk), .Q(d_ff_14_q));  // open: nQ
  and and_37 (and_37_out, not_26_out, and_36_out);
  and and_38 (and_38_out, d_ff_14_q, not_27_out);
  LED led_14 (.in(d_ff_14_q));
  not not_26 (not_26_out, d_ff_14_q);
  not not_27 (not_27_out, and_36_out);

  // Notes on the sheet:
  //   clk: Hz: 100
endmodule
