// Digital circuit Sinchronous_Counter Example JK.dig as structural Verilog
module Sinchronous_Counter_Example_JK (
  input  clk,
  input  in_2
);

  wire and_1_out, and_2_out, and_3_out, and_4_out, and_5_out, and_6_out, and_7_out, and_8_out, and_9_out,
       and_10_out, and_11_out, jk_ff_1_q, jk_ff_2_q, jk_ff_3_q, jk_ff_4_q, jk_ff_5_q, jk_ff_6_q, jk_ff_7_q,
       jk_ff_8_q, jk_ff_9_q, jk_ff_10_q, jk_ff_11_q, jk_ff_12_q, jk_ff_13_q;

  JK_FF jk_ff_1 (.J(in_2), .C(clk), .K(in_2), .Q(jk_ff_1_q));  // open: nQ
  and and_1 (and_1_out, jk_ff_1_q, jk_ff_2_q);
  JK_FF jk_ff_2 (.J(jk_ff_1_q), .C(clk), .K(jk_ff_1_q), .Q(jk_ff_2_q));  // open: nQ
  LED led_1 (.in(jk_ff_1_q));
  LED led_2 (.in(jk_ff_2_q));
  and and_2 (and_2_out, and_1_out, jk_ff_3_q);
  JK_FF jk_ff_3 (.J(and_1_out), .C(clk), .K(and_1_out), .Q(jk_ff_3_q));  // open: nQ
  LED led_3 (.in(jk_ff_3_q));
  and and_3 (and_3_out, and_2_out, jk_ff_4_q);
  JK_FF jk_ff_4 (.J(and_2_out), .C(clk), .K(and_2_out), .Q(jk_ff_4_q));  // open: nQ
  LED led_4 (.in(jk_ff_4_q));
  and and_4 (and_4_out, and_3_out, jk_ff_5_q);
  JK_FF jk_ff_5 (.J(and_3_out), .C(clk), .K(and_3_out), .Q(jk_ff_5_q));  // open: nQ
  and and_5 (and_5_out, and_4_out, jk_ff_6_q);
  JK_FF jk_ff_6 (.J(and_4_out), .C(clk), .K(and_4_out), .Q(jk_ff_6_q));  // open: nQ
  LED led_5 (.in(jk_ff_5_q));
  LED led_6 (.in(jk_ff_6_q));
  and and_6 (and_6_out, and_5_out, jk_ff_7_q);
  JK_FF jk_ff_7 (.J(and_5_out), .C(clk), .K(and_5_out), .Q(jk_ff_7_q));  // open: nQ
  LED led_7 (.in(jk_ff_7_q));
  and and_7 (and_7_out, and_6_out, jk_ff_8_q);
  JK_FF jk_ff_8 (.J(and_6_out), .C(clk), .K(and_6_out), .Q(jk_ff_8_q));  // open: nQ
  LED led_8 (.in(jk_ff_8_q));
  and and_8 (and_8_out, and_7_out, jk_ff_9_q);
  JK_FF jk_ff_9 (.J(and_7_out), .C(clk), .K(and_7_out), .Q(jk_ff_9_q));  // open: nQ
  and and_9 (and_9_out, and_8_out, jk_ff_10_q);
  JK_FF jk_ff_10 (.J(and_8_out), .C(clk), .K(and_8_out), .Q(jk_ff_10_q));  // open: nQ
  LED led_9 (.in(jk_ff_9_q));
  LED led_10 (.in(jk_ff_10_q));
  and and_10 (and_10_out, and_9_out, jk_ff_11_q);
  JK_FF jk_ff_11 (.J(and_9_out), .C(clk), .K(and_9_out), .Q(jk_ff_11_q));  // open: nQ
  LED led_11 (.in(jk_ff_11_q));
  and and_11 (and_11_out, and_10_out, jk_ff_12_q);
  JK_FF jk_ff_12 (.J(and_10_out), .C(clk), .K(and_10_out), .Q(jk_ff_12_q));  // open: nQ
  LED led_12 (.in(jk_ff_12_q));
  // And and_12 has open pins: In_1=and_11_out, In_2=jk_ff_13_q, out=open
  JK_FF jk_ff_13 (.J(and_11_out), .C(clk), .K(and_11_out), .Q(jk_ff_13_q));  // open: nQ
  LED led_13 (.in(jk_ff_13_q));

  // Notes on the sheet:
  //   clk: Hz: 100
endmodule
