// Digital circuit Somador_Completo_1_Bit Example.dig as structural Verilog
module Somador_Completo_1_Bit_Example (
  input  c_in,
  input  a,
  input  b,
  output out,
  output c_out
);

  wire and_1_out, and_2_out, and_3_out, xor_1_out;

  xor xor_1 (xor_1_out, a, b);
  and and_1 (and_1_out, c_in, a);
  and and_2 (and_2_out, c_in, b);
  and and_3 (and_3_out, a, b);
  xor xor_2 (out, c_in, xor_1_out);
  or or_1 (c_out, and_1_out, and_2_out, and_3_out);
endmodule
