// Digital circuit Somador_Completo_4_Bit Example.dig as structural Verilog
module Somador_Completo_4_Bit_Example (
  input  b_0,
  input  b_1,
  input  b_2,
  input  b_3,
  input  a_0,
  input  a_1,
  input  a_2,
  input  a_3,
  input  c_in,
  output out_0,
  output out_1,
  output out_2,
  output out_3,
  output c_out
);

  wire somador_completo_1_bit_example_1_c_out, somador_completo_1_bit_example_2_c_out,
       somador_completo_1_bit_example_3_c_out;

  Somador_Completo_1_Bit_Example somador_completo_1_bit_example_1 (
    .c_in(c_in), .a(a_0), .b(b_0), .out(out_0), .c_out(somador_completo_1_bit_example_1_c_out));
  Somador_Completo_1_Bit_Example somador_completo_1_bit_example_2 (
    .c_in(somador_completo_1_bit_example_1_c_out), .a(a_1), .b(b_1), .out(out_1),
    .c_out(somador_completo_1_bit_example_2_c_out));
  Somador_Completo_1_Bit_Example somador_completo_1_bit_example_3 (
    .c_in(somador_completo_1_bit_example_2_c_out), .a(a_2), .b(b_2), .out(out_2),
    .c_out(somador_completo_1_bit_example_3_c_out));
  Somador_Completo_1_Bit_Example somador_completo_1_bit_example_4 (
    .c_in(somador_completo_1_bit_example_3_c_out), .a(a_3), .b(b_3), .out(out_3), .c_out(c_out));
endmodule
