// Digital circuit Somador_Completo_4_Bit_Overflow Example.dig as structural Verilog
module Somador_Completo_4_Bit_Overflow_Example (
  input  c_in,
  input  b_0,
  input  b_1,
  input  b_2,
  input  b_3,
  input  a_0,
  input  a_1,
  input  a_2,
  input  a_3,
  output ovf,
  output out_0,
  output out_1,
  output out_2,
  output out_3,
  output c_out
);

  wire xnor_1_out;

  Somador_Completo_4_Bit_Example somador_completo_4_bit_example_1 (
    .b_0(b_0), .b_1(b_1), .b_2(b_2), .b_3(b_3), .a_0(a_0), .a_1(a_1), .a_2(a_2), .a_3(a_3), .c_in(c_in),
    .out_0(out_0), .out_1(out_1), .out_2(out_2), .out_3(out_3), .c_out(c_out));
  xnor xnor_1 (xnor_1_out, a_0, b_0);
  and and_1 (ovf, c_out, xnor_1_out);
endmodule
