// Digital circuit VHDL template.dig as structural Verilog
module VHDL_template (
  input  in_2,
  input  in_3,
  output out_1
);

  template #(.applicationType("GHDL")) u_template (.a(in_2), .b(in_3), .s(out_1));
endmodule

/* Code of template:
library IEEE;
  use IEEE.STD_LOGIC_1164.ALL;

-- Uncomment the following library declaration if using
-- arithmetic functions with Signed or Unsigned values
--use IEEE.NUMERIC_STD.ALL;

-- Uncomment the following library declaration if instantiating
-- any Xilinx leaf cells in this code.
--library UNISIM;
--use UNISIM.VComponents.all;

entity template is
  port( a: in std_logic;
	b: in std_logic;
	s: out std_logic);
end template;

architecture Behavioral of template is

begin

  s <= a and b;

end Behavioral;
*/
