// Digital circuit XOR Example.dig as structural Verilog
module XOR_Example (
  input  A,
  input  B,
  output S
);

  xor xor_1 (S, A, B);

  // Notes on the sheet:
  //   A: Entrada "A" do circuito XOR
  //   B: Entrada "B" do circuito XOR
  //   S: Saída "S" do circuito XOR
endmodule
