// Digital circuit converter_bcd_to_binary.dig as structural Verilog
module converter_bcd_to_binary (
  input  in_1,
  input  [7:0] in_2,
  input  in_3,
  input  clk,
  output out_5,
  output [3:0] out_6,
  output [3:0] out_7,
  output [3:0] out_8
);

  binary_to_bcd_converter #(.applicationType("GHDL")) u_binary_to_bcd_converter (
    .clk(clk), .rst(in_1), .str(in_3), .vin(in_2), .gobt(out_5), .vout0(out_6), .vout1(out_7), .vout2(out_8));

  // Notes on the sheet:
  //   in_2: default 168
  //   clk: Hz: 5
endmodule

/* Code of binary_to_bcd_converter:
library IEEE;
use IEEE.STD_LOGIC_1164.ALL;
use IEEE.NUMERIC_STD.ALL;

entity binary_to_bcd_converter is
    Port(
        clk : in std_logic;
        rst : in std_logic;
        str : in std_logic;
        vin : in std_logic_vector(7 downto 0);
        gobt : out std_logic;
        vout0 : out std_logic_vector(3 downto 0);
        vout1 : out std_logic_vector(3 downto 0);
        vout2 : out std_logic_vector(3 downto 0)
    );
end binary_to_bcd_converter;

architecture Behavioral of binary_to_bcd_converter is

    type states is (e0, e1, e2);
    signal current_st : states;
    signal s_ctr : std_logic_vector(2 downto 0);
    signal s_reg4_t1, s_reg4_t2, s_reg4_t3 : std_logic_vector(3 downto 0);
    signal s_regN_t : std_logic_vector(3 downto 0);

begin

    process(clk)
    begin
        if rst = '1' then
            current_st <= e0;
            gobt <= '0';
            s_ctr <= "000";
            s_reg4_t1 <= "0000";
            s_reg4_t2 <= "0000";
            s_reg4_t3 <= "0000";
            s_regN_t <= "0000";
            vout0 <= "0000";
            vout1 <= "0000";
            vout2 <= "0000";
        elsif rising_edge(clk) then
            case current_st is
                when e0 =>
                    if str = '1' then
                        gobt <= '0';
                        s_ctr <= "100";
                        s_regN_t <= vin(3 downto 0);
                        s_reg4_t1 <= vin(7 downto 4);
                        s_reg4_t2 <= "0000";
                        s_reg4_t3 <= "0000";
                        current_st <= e1;
                    else
                        current_st <= e0;
                        gobt <= '1';
                    end if;
                when e1 =>
                    if unsigned(s_reg4_t2) > 9 then
                        s_reg4_t2 <= std_logic_vector(unsigned(s_reg4_t2)-10);
                        s_reg4_t3 <= std_logic_vector(unsigned(s_reg4_t3)+1);
                        current_st <= e1;
                    elsif unsigned(s_reg4_t1) > 9 then
                        s_reg4_t1 <= std_logic_vector(unsigned(s_reg4_t1)-10);
                        s_reg4_t2 <= std_logic_vector(unsigned(s_reg4_t2)+1);
                        current_st <= e1;
                    elsif unsigned(s_ctr) > 0 then
                        s_reg4_t3 <= s_reg4_t3(2 downto 0) & s_reg4_t2(3);
                        s_reg4_t2 <= s_reg4_t2(2 downto 0) & s_reg4_t1(3);
                        s_reg4_t1 <= s_reg4_t1(2 downto 0) & s_regN_t(3);
                        s_regN_t <= s_regN_t(2 downto 0) & '0';
                        s_ctr <= std_logic_vector(unsigned(s_ctr)+1);
                        current_st <= e2;
                    else
                        current_st <= e0;
                        vout0 <= s_reg4_t1;
                        vout1 <= s_reg4_t2;
                        vout2 <= s_reg4_t3;
                        gobt <= '1';
                    end if;
                when e2 =>
                    if s_reg4_t3(0)='1' then
                        s_reg4_t2 <= std_logic_vector(unsigned(s_reg4_t2)+6);
                    end if;
                    if s_reg4_t2(0)='1' then
                        s_reg4_t1 <= std_logic_vector(unsigned(s_reg4_t1)+6);
                    end if;
                    current_st <= e1;
                when others =>
                    current_st <= e0;
            end case;
        end if;
    end process;

end Behavioral;
*/
