// Digital circuit DecodificadorHEXBCD.dig as structural Verilog
module DecodificadorHEXBCD (
  input  [7:0] in,
  output [3:0] out_1,
  output [3:0] out_2,
  output [3:0] out_3
);

  Seven_Seg_Hex seven_seg_hex_1 (.d(out_3), .dp(1'b0));
  Seven_Seg_Hex seven_seg_hex_2 (.d(out_2), .dp(1'b0));
  Seven_Seg_Hex seven_seg_hex_3 (.d(out_1), .dp(1'b0));
endmodule
