// Digital circuit NAND.dig as structural Verilog
module NAND (
  input  A,
  input  B,
  output Q
);

  wire nfet_1_s;

  PFET pfet_1 (.G(A), .S(1'b1), .D(Q));
  NFET nfet_1 (.G(A), .D(Q), .S(nfet_1_s));
  NFET nfet_2 (.G(B), .D(nfet_1_s), .S(1'b0));
  PFET pfet_2 (.G(B), .S(1'b1), .D(Q));
endmodule
