// Digital circuit NOR.dig as structural Verilog
module NOR (
  input  A,
  input  B,
  output Q
);

  wire pfet_1_d;

  NFET nfet_1 (.G(A), .D(Q), .S(1'b0));
  PFET pfet_1 (.G(A), .S(1'b1), .D(pfet_1_d));
  PFET pfet_2 (.G(B), .S(pfet_1_d), .D(Q));
  NFET nfet_2 (.G(B), .D(Q), .S(1'b0));
endmodule
