// Digital circuit XOR.dig as structural Verilog
module XOR (
  input  A,
  input  B,
  output Q
);

  wire A_t, B_t, nfet_1_s, nfet_3_s, pfet_1_d;

  PFET pfet_1 (.G(A), .S(1'b1), .D(pfet_1_d));
  PFET pfet_2 (.G(B_t), .S(pfet_1_d), .D(Q));
  NFET nfet_1 (.G(B), .D(Q), .S(nfet_1_s));
  NFET nfet_2 (.G(A), .D(nfet_1_s), .S(1'b0));
  NOT not_1 (.Q_2(A), .Q(A_t));
  NOT not_2 (.Q_2(B), .Q(B_t));
  PFET pfet_3 (.G(B), .S(1'b1), .D(pfet_1_d));
  PFET pfet_4 (.G(A_t), .S(pfet_1_d), .D(Q));
  NFET nfet_3 (.G(B_t), .D(Q), .S(nfet_3_s));
  NFET nfet_4 (.G(A_t), .D(nfet_3_s), .S(1'b0));
endmodule
