// Digital circuit test.dig as structural Verilog
module test (
  input  A,
  input  B,
  output AB,
  output A_plus_B,
  output A_2,
  output A__x__B
);

  NAND nand_1 (.A(A), .B(B), .Q(AB));
  NOR nor_1 (.A(A), .B(B), .Q(A_plus_B));
  NOT not_1 (.Q_2(A), .Q(A_2));
  XOR xor_1 (.A(A), .B(B), .Q(A__x__B));
endmodule
