// Digital circuit ALU.dig as structural Verilog
module ALU (
  input  [3:0] op,
  input  [7:0] in_2,
  input  [7:0] in_1,
  input  [7:0] kk,
  output [7:0] out,
  output Z,
  output C,
  output P
);

  // NotConnected on in_1[0]
  // NotConnected on in_2[0]
  // NotConnected on kk[0]
  // NotConnected on op[0]
  // Pins of 1 and 4 bits meet at op
  // Pins of 1 and 8 bits meet at in_2
  // Pins of 1 and 8 bits meet at in_1
  // Pins of 1 and 8 bits meet at kk

  assign C = 1'b0;
  assign out = {8{1'b0}};
  assign P = 1'b0;
  assign Z = 1'b0;
endmodule
