// Digital circuit KCPSM3.dig as structural Verilog
module KCPSM3 (
  input  [7:0] inPort,
  output outPort
);

  wire alu_1_c, alu_1_p, alu_1_z, opid_1_p2, pfc_1_pc, zcf_1_c_out, zcf_1_z_out;
  wire [7:0] alu_1_out, multiplexer_1_out, spm_1_p1;
  wire [9:0] pc_1_a;
  wire [17:0] ramsingleport_1_d;

  Multiplexer #(.Bits(8), .Selector_Bits(2)) multiplexer_1 (
    .in_0(alu_1_out), .in_1(inPort), .in_2(spm_1_p1), .in_3({8{1'b0}}), .out(multiplexer_1_out));  // open: sel
  RegisterFile registerfile_1 (.Din(multiplexer_1_out[0]));  // open: we, Rw, C, Ra, Rb, Da, Db
  // SPM spm_1: pin names not known; wires that end beside it: spm_1_p1, outPort
  RAMSinglePort #(.AddrBits(10), .Bits(18)) ramsingleport_1 (
    .A(pc_1_a), .str(1'b0), .ld(1'b0), .D(ramsingleport_1_d));  // open: C
  ALU alu_1 (.out(alu_1_out), .Z(alu_1_z), .C(alu_1_c), .P(alu_1_p));  // open: op, in_2, in_1, kk
  PAC pac_1 ();  // open: p, in, clk, pid, ws, rs
  ZCf zcf_1 (.Z_in(alu_1_z), .C_in(alu_1_c), .P_in(alu_1_p), .Z_out(zcf_1_z_out), .C_out(zcf_1_c_out));  // open: clk
  // OPID opid_1: pin names not known; wires that end beside it: ramsingleport_1_d, opid_1_p2
  PFC pfc_1 (.Z(zcf_1_z_out), .C(zcf_1_c_out), .a(opid_1_p2), .PC(pfc_1_pc));  // open: clk
  PC pc_1 (.PC_in(pfc_1_pc), .A(pc_1_a));
  PCS pcs_1 (.PC_in(pfc_1_pc));  // open: PC_out
  // Pins of 1 and 8 bits meet at multiplexer_1_out
  // Pins of 1 and 8 bits meet at inPort
endmodule
