// Digital circuit meio_somador_4_bits.dig as structural Verilog
module meio_somador_4_bits (
  input  [3:0] in_1,
  input  [3:0] in_2,
  output [3:0] out,
  output c_out
);

  wire meio_somador_2_bits_1_c_out;

  meio_somador_2_bits meio_somador_2_bits_1 (
    .in1(in_1[1:0]), .in2(in_2[3:2]), .out(out[1:0]), .c_out(meio_somador_2_bits_1_c_out));
  somador_2_bits somador_2_bits_1 (
    .in1(in_1[3:2]), .in2(in_2[3:2]), .c_in(meio_somador_2_bits_1_c_out), .out(out[3:2]), .c_out(c_out));

  assign in_2[1:0] = in_2[3:2];
endmodule
