// Digital circuit meio_somador_2_bits.dig as structural Verilog
module meio_somador_2_bits (
  input  [1:0] in1,
  input  [1:0] in2,
  output [1:0] out,
  output c_out
);

  wire meio_somador_1_bit_1_c_out;

  meio_somador_1_bit meio_somador_1_bit_1 (
    .in_1(in1[0]), .in_2(in2[0]), .out(out[0]), .c_out(meio_somador_1_bit_1_c_out));
  somador_1_bit somador_1_bit_1 (
    .in_1(in1[1]), .in_2(in2[1]), .c_in(meio_somador_1_bit_1_c_out), .out(out[1]), .c_out(c_out));
endmodule
