// Digital circuit meio_somador_1_bit.dig as structural Verilog
module meio_somador_1_bit (
  input  in_1,
  input  in_2,
  output out,
  output c_out
);

  xor xor_1 (out, in_1, in_2);
  and and_1 (c_out, in_1, in_2);
endmodule
