// Digital circuit somador_1_bit.dig as structural Verilog
module somador_1_bit (
  input  in_1,
  input  in_2,
  input  c_in,
  output out,
  output c_out
);

  wire and_1_out, and_2_out, xor_1_out;

  xor xor_1 (xor_1_out, in_1, in_2);
  and and_1 (and_1_out, in_1, in_2);
  xor xor_2 (out, c_in, xor_1_out);
  and and_2 (and_2_out, c_in, xor_1_out);
  or or_1 (c_out, and_2_out, and_1_out);
endmodule
