// Digital circuit somador_2_bits.dig as structural Verilog
module somador_2_bits (
  input  [1:0] in1,
  input  [1:0] in2,
  input  c_in,
  output [1:0] out,
  output c_out
);

  wire somador_1_bit_1_c_out;

  somador_1_bit somador_1_bit_1 (
    .in_1(in1[0]), .in_2(in2[0]), .c_in(c_in), .out(out[0]), .c_out(somador_1_bit_1_c_out));
  somador_1_bit somador_1_bit_2 (
    .in_1(in1[1]), .in_2(in2[1]), .c_in(somador_1_bit_1_c_out), .out(out[1]), .c_out(c_out));
endmodule
