// Digital circuit ALU.dig as structural Verilog
module ALU (
  input  [7:0] in_1,
  input  [7:0] in_2,
  input  [3:0] op,
  input  C_i,
  output [7:0] out,
  output Z,
  output C_o
);

  wire [8:0] add_1_out;

  ADD add_1 (.in_1(in_1), .in_2(in_2), .C_in(C_i), .out(add_1_out));
  Multiplexer #(.Selector_Bits(4), .Bits(9)) multiplexer_1 (
    .sel(op), .in_0({9{1'b0}}), .in_1({1'b0, in_2}), .in_2({9{1'b0}}), .in_3({9{1'b0}}), .in_4({9{1'b0}}),
    .in_5(add_1_out), .in_6(add_1_out), .in_7({9{1'b0}}), .in_8({9{1'b0}}), .in_9({9{1'b0}}),
    .in_10({9{1'b0}}), .in_11({9{1'b0}}), .in_12({9{1'b0}}), .in_13({9{1'b0}}), .in_14({9{1'b0}}),
    .in_15({9{1'b0}}), .out({C_o, out}));
  and and_1 (Z, ~out[0], ~out[1], ~out[2], ~out[3], ~out[4], ~out[5], ~out[6], ~out[7]);  // And
endmodule
