// Digital circuit RR.dig as structural Verilog
module RR (
  input  [7:0] in,
  output [8:0] out
);

  // Pins of 8 and 9 bits meet at {{2{in[0]}}, in[7:1]}

  assign out = {{2{in[0]}}, in[7:1]};
endmodule
