// Digital circuit SLA.dig as structural Verilog
module SLA (
  input  [7:0] in,
  input  C_in,
  output [8:0] out
);

  // Pins of 8 and 9 bits meet at {in, C_in}

  assign out = {in, C_in};
endmodule
