// Digital circuit SRA.dig as structural Verilog
module SRA (
  input  [7:0] in,
  input  C_in,
  output [8:0] out
);

  // Pins of 8 and 9 bits meet at {in[0], C_in, in[7:1]}

  assign out = {in[0], C_in, in[7:1]};
endmodule
