// Digital circuit PCStack.dig as structural Verilog
module PCStack (
  input  [9:0] in,
  input  sel,
  input  EN,
  input  clk,
  output C,
  output [9:0] out,
  output [4:0] N
);

  wire and_1_out, and_2_out, demultiplexer_1_out_0, demultiplexer_1_out_1, demultiplexer_1_out_2,
       demultiplexer_1_out_3, demultiplexer_1_out_4, demultiplexer_1_out_5, demultiplexer_1_out_6,
       demultiplexer_1_out_7, demultiplexer_4_out_0, demultiplexer_4_out_1, demultiplexer_4_out_2,
       demultiplexer_4_out_3, demultiplexer_5_out_0, demultiplexer_5_out_1, demultiplexer_5_out_2,
       demultiplexer_5_out_3, demultiplexer_6_out_0, demultiplexer_6_out_1, demultiplexer_6_out_2,
       demultiplexer_6_out_3, demultiplexer_7_out_0, demultiplexer_7_out_1, demultiplexer_7_out_2,
       demultiplexer_7_out_3, demultiplexer_8_out_0, demultiplexer_8_out_1, demultiplexer_8_out_2,
       demultiplexer_8_out_3, demultiplexer_9_out_0, demultiplexer_9_out_1, demultiplexer_9_out_2,
       demultiplexer_9_out_3, demultiplexer_10_out_0, demultiplexer_10_out_1, demultiplexer_10_out_2,
       demultiplexer_10_out_3, demultiplexer_11_out_0, demultiplexer_11_out_1, demultiplexer_11_out_2,
       demultiplexer_11_out_3, pcstack_add1_1_c, pcstack_sub1_1_c;
  wire [1:0] demultiplexer_2_out_0, demultiplexer_2_out_1, demultiplexer_2_out_2, demultiplexer_2_out_3,
       demultiplexer_2_out_4, demultiplexer_2_out_5, demultiplexer_2_out_6, demultiplexer_2_out_7;
  wire [2:0] demultiplexer_3_out_0, demultiplexer_3_out_1, demultiplexer_3_out_2, demultiplexer_3_out_3;
  wire [4:0] multiplexer_1_out, pcstack_add1_1_out, pcstack_sub1_1_out;
  wire [9:0] multiplexer_2_out, multiplexer_3_out, multiplexer_4_out, multiplexer_5_out, register_1_q,
       register_2_q, register_3_q, register_4_q, register_5_q, register_6_q, register_7_q, register_8_q,
       register_9_q, register_10_q, register_11_q, register_12_q, register_13_q, register_14_q,
       register_15_q, register_16_q, register_17_q, register_18_q, register_19_q, register_20_q,
       register_21_q, register_22_q, register_23_q, register_24_q, register_25_q, register_26_q,
       register_27_q, register_28_q, register_29_q, register_30_q, register_31_q, register_32_q;

  Multiplexer #(.Bits(5)) multiplexer_1 (
    .sel(sel), .in_0(pcstack_sub1_1_out), .in_1(pcstack_add1_1_out), .out(multiplexer_1_out));
  Register #(.Bits(5)) PC_Stack_Counter (.D(multiplexer_1_out), .C(clk), .en(EN), .Q(N));
  PCStack_Add1 pcstack_add1_1 (.in(N), .out(pcstack_add1_1_out), .C(pcstack_add1_1_c));
  PCStack_Sub1 pcstack_sub1_1 (.in(N), .out(pcstack_sub1_1_out), .C(pcstack_sub1_1_c));
  and and_1 (and_1_out, EN, sel, pcstack_add1_1_c);
  and and_2 (and_2_out, EN, ~sel, pcstack_sub1_1_c);  // And
  or or_1 (C, and_1_out, and_2_out);
  Demultiplexer #(.Selector_Bits(3)) demultiplexer_1 (
    .sel(N[4:2]), .in(sel), .out_0(demultiplexer_1_out_0), .out_1(demultiplexer_1_out_1),
    .out_2(demultiplexer_1_out_2), .out_3(demultiplexer_1_out_3), .out_4(demultiplexer_1_out_4),
    .out_5(demultiplexer_1_out_5), .out_6(demultiplexer_1_out_6), .out_7(demultiplexer_1_out_7));
  Demultiplexer #(.Selector_Bits(3), .Bits(2)) demultiplexer_2 (
    .sel(N[4:2]), .in(N[1:0]), .out_0(demultiplexer_2_out_0), .out_1(demultiplexer_2_out_1),
    .out_2(demultiplexer_2_out_2), .out_3(demultiplexer_2_out_3), .out_4(demultiplexer_2_out_4),
    .out_5(demultiplexer_2_out_5), .out_6(demultiplexer_2_out_6), .out_7(demultiplexer_2_out_7));
  Demultiplexer #(.Selector_Bits(2), .Bits(3)) demultiplexer_3 (
    .sel(pcstack_sub1_1_out[1:0]), .in(pcstack_sub1_1_out[4:2]), .out_0(demultiplexer_3_out_0),
    .out_1(demultiplexer_3_out_1), .out_2(demultiplexer_3_out_2), .out_3(demultiplexer_3_out_3));
  Demultiplexer #(.Selector_Bits(2)) demultiplexer_4 (
    .sel(demultiplexer_2_out_0), .in(demultiplexer_1_out_0), .out_0(demultiplexer_4_out_0),
    .out_1(demultiplexer_4_out_1), .out_2(demultiplexer_4_out_2), .out_3(demultiplexer_4_out_3));
  Demultiplexer #(.Selector_Bits(2)) demultiplexer_5 (
    .sel(demultiplexer_2_out_1), .in(demultiplexer_1_out_1), .out_0(demultiplexer_5_out_0),
    .out_1(demultiplexer_5_out_1), .out_2(demultiplexer_5_out_2), .out_3(demultiplexer_5_out_3));
  Demultiplexer #(.Selector_Bits(2)) demultiplexer_6 (
    .sel(demultiplexer_2_out_2), .in(demultiplexer_1_out_2), .out_0(demultiplexer_6_out_0),
    .out_1(demultiplexer_6_out_1), .out_2(demultiplexer_6_out_2), .out_3(demultiplexer_6_out_3));
  Demultiplexer #(.Selector_Bits(2)) demultiplexer_7 (
    .sel(demultiplexer_2_out_3), .in(demultiplexer_1_out_3), .out_0(demultiplexer_7_out_0),
    .out_1(demultiplexer_7_out_1), .out_2(demultiplexer_7_out_2), .out_3(demultiplexer_7_out_3));
  Demultiplexer #(.Selector_Bits(2)) demultiplexer_8 (
    .sel(demultiplexer_2_out_4), .in(demultiplexer_1_out_4), .out_0(demultiplexer_8_out_0),
    .out_1(demultiplexer_8_out_1), .out_2(demultiplexer_8_out_2), .out_3(demultiplexer_8_out_3));
  Demultiplexer #(.Selector_Bits(2)) demultiplexer_9 (
    .sel(demultiplexer_2_out_5), .in(demultiplexer_1_out_5), .out_0(demultiplexer_9_out_0),
    .out_1(demultiplexer_9_out_1), .out_2(demultiplexer_9_out_2), .out_3(demultiplexer_9_out_3));
  Demultiplexer #(.Selector_Bits(2)) demultiplexer_10 (
    .sel(demultiplexer_2_out_6), .in(demultiplexer_1_out_6), .out_0(demultiplexer_10_out_0),
    .out_1(demultiplexer_10_out_1), .out_2(demultiplexer_10_out_2), .out_3(demultiplexer_10_out_3));
  Demultiplexer #(.Selector_Bits(2)) demultiplexer_11 (
    .sel(demultiplexer_2_out_7), .in(demultiplexer_1_out_7), .out_0(demultiplexer_11_out_0),
    .out_1(demultiplexer_11_out_1), .out_2(demultiplexer_11_out_2), .out_3(demultiplexer_11_out_3));
  Register #(.Bits(10)) register_1 (.D(in), .C(clk), .en(demultiplexer_4_out_0), .Q(register_1_q));
  Register #(.Bits(10)) register_2 (.D(in), .C(clk), .en(demultiplexer_5_out_0), .Q(register_2_q));
  Register #(.Bits(10)) register_3 (.D(in), .C(clk), .en(demultiplexer_6_out_0), .Q(register_3_q));
  Register #(.Bits(10)) register_4 (.D(in), .C(clk), .en(demultiplexer_7_out_0), .Q(register_4_q));
  Register #(.Bits(10)) register_5 (.D(in), .C(clk), .en(demultiplexer_8_out_0), .Q(register_5_q));
  Register #(.Bits(10)) register_6 (.D(in), .C(clk), .en(demultiplexer_9_out_0), .Q(register_6_q));
  Register #(.Bits(10)) register_7 (.D(in), .C(clk), .en(demultiplexer_10_out_0), .Q(register_7_q));
  Register #(.Bits(10)) register_8 (.D(in), .C(clk), .en(demultiplexer_11_out_0), .Q(register_8_q));
  // Probe on register_1_q
  // Probe on register_2_q
  // Probe on register_3_q
  // Probe on register_4_q
  Multiplexer #(.Selector_Bits(3), .Bits(10)) multiplexer_2 (
    .sel(demultiplexer_3_out_0), .in_0(register_1_q), .in_1(register_2_q), .in_2(register_3_q),
    .in_3(register_4_q), .in_4(register_5_q), .in_5(register_6_q), .in_6(register_7_q), .in_7(register_8_q),
    .out(multiplexer_2_out));
  Register #(.Bits(10)) register_9 (.D(in), .C(clk), .en(demultiplexer_4_out_1), .Q(register_9_q));
  Register #(.Bits(10)) register_10 (.D(in), .C(clk), .en(demultiplexer_5_out_1), .Q(register_10_q));
  Register #(.Bits(10)) register_11 (.D(in), .C(clk), .en(demultiplexer_6_out_1), .Q(register_11_q));
  Register #(.Bits(10)) register_12 (.D(in), .C(clk), .en(demultiplexer_7_out_1), .Q(register_12_q));
  Register #(.Bits(10)) register_13 (.D(in), .C(clk), .en(demultiplexer_8_out_1), .Q(register_13_q));
  Register #(.Bits(10)) register_14 (.D(in), .C(clk), .en(demultiplexer_9_out_1), .Q(register_14_q));
  Register #(.Bits(10)) register_15 (.D(in), .C(clk), .en(demultiplexer_10_out_1), .Q(register_15_q));
  Register #(.Bits(10)) register_16 (.D(in), .C(clk), .en(demultiplexer_11_out_1), .Q(register_16_q));
  // Probe on register_9_q
  // Probe on register_10_q
  // Probe on register_11_q
  // Probe on register_12_q
  Multiplexer #(.Selector_Bits(3), .Bits(10)) multiplexer_3 (
    .sel(demultiplexer_3_out_1), .in_0(register_9_q), .in_1(register_10_q), .in_2(register_11_q),
    .in_3(register_12_q), .in_4(register_13_q), .in_5(register_14_q), .in_6(register_15_q),
    .in_7(register_16_q), .out(multiplexer_3_out));
  Register #(.Bits(10)) register_17 (.D(in), .C(clk), .en(demultiplexer_4_out_2), .Q(register_17_q));
  Register #(.Bits(10)) register_18 (.D(in), .C(clk), .en(demultiplexer_5_out_2), .Q(register_18_q));
  Register #(.Bits(10)) register_19 (.D(in), .C(clk), .en(demultiplexer_6_out_2), .Q(register_19_q));
  Register #(.Bits(10)) register_20 (.D(in), .C(clk), .en(demultiplexer_7_out_2), .Q(register_20_q));
  Register #(.Bits(10)) register_21 (.D(in), .C(clk), .en(demultiplexer_8_out_2), .Q(register_21_q));
  Register #(.Bits(10)) register_22 (.D(in), .C(clk), .en(demultiplexer_9_out_2), .Q(register_22_q));
  Register #(.Bits(10)) register_23 (.D(in), .C(clk), .en(demultiplexer_10_out_2), .Q(register_23_q));
  Register #(.Bits(10)) register_24 (.D(in), .C(clk), .en(demultiplexer_11_out_2), .Q(register_24_q));
  // Probe on register_17_q
  // Probe on register_18_q
  // Probe on register_19_q
  // Probe on register_20_q
  Multiplexer #(.Selector_Bits(3), .Bits(10)) multiplexer_4 (
    .sel(demultiplexer_3_out_2), .in_0(register_17_q), .in_1(register_18_q), .in_2(register_19_q),
    .in_3(register_20_q), .in_4(register_21_q), .in_5(register_22_q), .in_6(register_23_q),
    .in_7(register_24_q), .out(multiplexer_4_out));
  Register #(.Bits(10)) register_25 (.D(in), .C(clk), .en(demultiplexer_4_out_3), .Q(register_25_q));
  Register #(.Bits(10)) register_26 (.D(in), .C(clk), .en(demultiplexer_5_out_3), .Q(register_26_q));
  Register #(.Bits(10)) register_27 (.D(in), .C(clk), .en(demultiplexer_6_out_3), .Q(register_27_q));
  Register #(.Bits(10)) register_28 (.D(in), .C(clk), .en(demultiplexer_7_out_3), .Q(register_28_q));
  Register #(.Bits(10)) register_29 (.D(in), .C(clk), .en(demultiplexer_8_out_3), .Q(register_29_q));
  Register #(.Bits(10)) register_30 (.D(in), .C(clk), .en(demultiplexer_9_out_3), .Q(register_30_q));
  Register #(.Bits(10)) register_31 (.D(in), .C(clk), .en(demultiplexer_10_out_3), .Q(register_31_q));
  Register #(.Bits(10)) register_32 (.D(in), .C(clk), .en(demultiplexer_11_out_3), .Q(register_32_q));
  // Probe on register_25_q
  // Probe on register_26_q
  // Probe on register_27_q
  // Probe on register_28_q
  Multiplexer #(.Selector_Bits(3), .Bits(10)) multiplexer_5 (
    .sel(demultiplexer_3_out_3), .in_0(register_25_q), .in_1(register_26_q), .in_2(register_27_q),
    .in_3(register_28_q), .in_4(register_29_q), .in_5(register_30_q), .in_6(register_31_q),
    .in_7(register_32_q), .out(multiplexer_5_out));
  Multiplexer #(.Selector_Bits(2), .Bits(10)) multiplexer_6 (
    .sel(pcstack_sub1_1_out[1:0]), .in_0(multiplexer_2_out), .in_1(multiplexer_3_out),
    .in_2(multiplexer_4_out), .in_3(multiplexer_5_out), .out(out));
endmodule
