// Digital circuit ProgramController.dig as structural Verilog
module ProgramController (
  input  [4:0] Instruction,
  input  EN,
  output [11:0] out
);

  wire ContrAddress, ContrFlag1, ContrFlag2, ContrSP, EW, InterruptFlag, ReadWrite, UpdateFlags;
  wire [3:0] op;
  wire [11:0] bitextender_1_out;

  Multiplexer #(.Selector_Bits(5), .Bits(4)) multiplexer_1 (
    .sel(Instruction), .in_0(4'b0000), .in_1(4'b0001), .in_2(4'b0010), .in_3(4'b0011), .in_4(4'b0100),
    .in_5(4'b0010), .in_6(4'b0101), .in_7(4'b0101), .in_8(4'b0110), .in_9(4'b0110), .in_10(4'b0100),
    .in_11(4'b0111), .in_12(4'b0111), .in_13(4'b1000), .in_14(4'b0111), .in_15(4'b1001), .in_16(4'b1010),
    .in_17(4'b1010), .in_18(4'b1011), .in_19(4'b1010), .in_20(4'b1100), .in_21(4'b0000), .in_22(4'b0000),
    .in_23(4'b0000), .in_24(4'b0000), .in_25(4'b0000), .in_26(4'b0000), .in_27(4'b0000), .in_28(4'b0000),
    .in_29(4'b0000), .in_30(4'b0000), .in_31(4'b0000), .out(op));
  Multiplexer #(.Selector_Bits(5)) multiplexer_2 (
    .sel(Instruction), .in_0(1'b0), .in_1(1'b0), .in_2(1'b1), .in_3(1'b1), .in_4(1'b1), .in_5(1'b1),
    .in_6(1'b1), .in_7(1'b1), .in_8(1'b1), .in_9(1'b1), .in_10(1'b1), .in_11(1'b1), .in_12(1'b1),
    .in_13(1'b1), .in_14(1'b1), .in_15(1'b1), .in_16(1'b1), .in_17(1'b1), .in_18(1'b1), .in_19(1'b1),
    .in_20(1'b1), .in_21(1'b0), .in_22(1'b0), .in_23(1'b0), .in_24(1'b0), .in_25(1'b0), .in_26(1'b0),
    .in_27(1'b0), .in_28(1'b0), .in_29(1'b1), .in_30(1'b0), .in_31(1'b0), .out(UpdateFlags));
  Multiplexer #(.Selector_Bits(5)) multiplexer_3 (
    .sel(Instruction), .in_0(1'b0), .in_1(1'b1), .in_2(1'b1), .in_3(1'b1), .in_4(1'b1), .in_5(1'b0),
    .in_6(1'b1), .in_7(1'b1), .in_8(1'b1), .in_9(1'b1), .in_10(1'b0), .in_11(1'b1), .in_12(1'b1),
    .in_13(1'b1), .in_14(1'b1), .in_15(1'b1), .in_16(1'b1), .in_17(1'b1), .in_18(1'b1), .in_19(1'b1),
    .in_20(1'b1), .in_21(1'b1), .in_22(1'b0), .in_23(1'b0), .in_24(1'b0), .in_25(1'b0), .in_26(1'b0),
    .in_27(1'b1), .in_28(1'b0), .in_29(1'b0), .in_30(1'b0), .in_31(1'b0), .out(EW));
  Multiplexer #(.Selector_Bits(5)) multiplexer_4 (
    .sel(Instruction), .in_0(1'b0), .in_1(1'b0), .in_2(1'b0), .in_3(1'b0), .in_4(1'b0), .in_5(1'b0),
    .in_6(1'b0), .in_7(1'b0), .in_8(1'b0), .in_9(1'b0), .in_10(1'b0), .in_11(1'b0), .in_12(1'b0),
    .in_13(1'b0), .in_14(1'b0), .in_15(1'b0), .in_16(1'b0), .in_17(1'b0), .in_18(1'b0), .in_19(1'b0),
    .in_20(1'b0), .in_21(1'b1), .in_22(1'b1), .in_23(1'b0), .in_24(1'b0), .in_25(1'b0), .in_26(1'b0),
    .in_27(1'b0), .in_28(1'b0), .in_29(1'b0), .in_30(1'b0), .in_31(1'b0), .out(ReadWrite));
  BitExtender #(.inputBits(1), .outputBits(12)) bitextender_1 (.in(EN), .out(bitextender_1_out));
  assign out = {ContrSP, InterruptFlag, ContrFlag2, ContrFlag1, ContrAddress, ReadWrite, EW, UpdateFlags, op} & bitextender_1_out;  // And and_1, 12 bits wide
  Multiplexer #(.Selector_Bits(5)) multiplexer_5 (
    .sel(Instruction), .in_0(1'b0), .in_1(1'b0), .in_2(1'b0), .in_3(1'b0), .in_4(1'b0), .in_5(1'b0),
    .in_6(1'b0), .in_7(1'b0), .in_8(1'b0), .in_9(1'b0), .in_10(1'b0), .in_11(1'b0), .in_12(1'b0),
    .in_13(1'b0), .in_14(1'b0), .in_15(1'b0), .in_16(1'b0), .in_17(1'b0), .in_18(1'b0), .in_19(1'b0),
    .in_20(1'b0), .in_21(1'b0), .in_22(1'b0), .in_23(1'b1), .in_24(1'b1), .in_25(1'b1), .in_26(1'b0),
    .in_27(1'b0), .in_28(1'b0), .in_29(1'b1), .in_30(1'b0), .in_31(1'b0), .out(ContrAddress));
  Multiplexer #(.Selector_Bits(5)) multiplexer_6 (
    .sel(Instruction), .in_0(1'b0), .in_1(1'b0), .in_2(1'b0), .in_3(1'b0), .in_4(1'b0), .in_5(1'b0),
    .in_6(1'b1), .in_7(1'b0), .in_8(1'b1), .in_9(1'b0), .in_10(1'b0), .in_11(1'b1), .in_12(1'b1),
    .in_13(1'b0), .in_14(1'b0), .in_15(1'b0), .in_16(1'b1), .in_17(1'b1), .in_18(1'b0), .in_19(1'b0),
    .in_20(1'b0), .in_21(1'b0), .in_22(1'b1), .in_23(1'b0), .in_24(1'b1), .in_25(1'b1), .in_26(1'b1),
    .in_27(1'b0), .in_28(1'b1), .in_29(1'b1), .in_30(1'b0), .in_31(1'b0), .out(ContrFlag1));
  Multiplexer #(.Selector_Bits(5)) multiplexer_7 (
    .sel(Instruction), .in_0(1'b0), .in_1(1'b0), .in_2(1'b0), .in_3(1'b0), .in_4(1'b0), .in_5(1'b0),
    .in_6(1'b0), .in_7(1'b0), .in_8(1'b0), .in_9(1'b0), .in_10(1'b0), .in_11(1'b0), .in_12(1'b1),
    .in_13(1'b0), .in_14(1'b0), .in_15(1'b0), .in_16(1'b0), .in_17(1'b1), .in_18(1'b0), .in_19(1'b0),
    .in_20(1'b0), .in_21(1'b0), .in_22(1'b0), .in_23(1'b1), .in_24(1'b1), .in_25(1'b0), .in_26(1'b0),
    .in_27(1'b0), .in_28(1'b0), .in_29(1'b0), .in_30(1'b0), .in_31(1'b0), .out(ContrFlag2));
  Multiplexer #(.Selector_Bits(5)) multiplexer_8 (
    .sel(Instruction), .in_0(1'b0), .in_1(1'b0), .in_2(1'b0), .in_3(1'b0), .in_4(1'b0), .in_5(1'b0),
    .in_6(1'b0), .in_7(1'b0), .in_8(1'b0), .in_9(1'b0), .in_10(1'b0), .in_11(1'b0), .in_12(1'b0),
    .in_13(1'b0), .in_14(1'b0), .in_15(1'b0), .in_16(1'b0), .in_17(1'b0), .in_18(1'b0), .in_19(1'b0),
    .in_20(1'b0), .in_21(1'b0), .in_22(1'b0), .in_23(1'b0), .in_24(1'b0), .in_25(1'b0), .in_26(1'b0),
    .in_27(1'b0), .in_28(1'b1), .in_29(1'b1), .in_30(1'b1), .in_31(1'b0), .out(InterruptFlag));
  Multiplexer #(.Selector_Bits(5)) multiplexer_9 (
    .sel(Instruction), .in_0(1'b0), .in_1(1'b0), .in_2(1'b0), .in_3(1'b0), .in_4(1'b0), .in_5(1'b0),
    .in_6(1'b0), .in_7(1'b0), .in_8(1'b0), .in_9(1'b0), .in_10(1'b0), .in_11(1'b0), .in_12(1'b0),
    .in_13(1'b0), .in_14(1'b0), .in_15(1'b0), .in_16(1'b0), .in_17(1'b0), .in_18(1'b0), .in_19(1'b0),
    .in_20(1'b0), .in_21(1'b0), .in_22(1'b0), .in_23(1'b0), .in_24(1'b0), .in_25(1'b0), .in_26(1'b1),
    .in_27(1'b1), .in_28(1'b0), .in_29(1'b0), .in_30(1'b0), .in_31(1'b0), .out(ContrSP));

  // Notes on the sheet:
  //   LOAD
  //   OR
  //   TEST
  //   ADDCY
  //   SUBCY
  //   SR0
  //   SRX
  //   RR
  //   SL1
  //   SLA
  //   INPUT
  //   JUMP
  //   RETURN
  //   FETCH
  //   RETURNI
  //   HALT
  //   AND
  //   XOR
  //   ADD
  //   SUB
  //   COMPARE
  //   SR1
  //   SRA
  //   SL0
  //   SLX
  //   RL
  //   OUTPUT
  //   CALL
  //   STORE
  //   ENABLE INT
  //   ISRADDRESS
endmodule
