// Digital circuit processor.dig as structural Verilog
module processor (
  input  clk,
  input  [7:0] Read
);

  wire and_1_out, BRAM, decoder_1_out_0, decoder_1_out_1, decoder_1_out_2, decoder_1_out_3, decoder_1_out_4,
       decoder_1_out_5, decoder_1_out_6, decoder_1_out_7, decoder_1_out_8, decoder_1_out_9, decoder_1_out_10,
       decoder_1_out_11, decoder_1_out_12, decoder_1_out_13, decoder_1_out_14, decoder_1_out_15,
       decoder_1_out_16, decoder_1_out_17, decoder_1_out_18, decoder_1_out_19, decoder_1_out_20,
       decoder_1_out_21, decoder_1_out_22, decoder_1_out_23, decoder_1_out_24, decoder_1_out_25,
       decoder_1_out_26, decoder_1_out_27, decoder_1_out_28, decoder_1_out_29, decoder_1_out_30,
       decoder_1_out_31, Int, Int_Ack, Int_E, jk_ff_1_nq, jk_ff_2_q, not_1_out, or_1_out, PC_Ovf, RS,
       SendInt, Stack_Ovf, WS;
  wire [4:0] Instruction;
  wire [7:0] PortID, register_1_q, register_2_q, register_3_q, Write;
  wire [9:0] Address;
  wire [17:0] Program_Instructions_d;

  Seven_Seg_Hex seven_seg_hex_1 (.d({2'b00, Address[9:8]}), .dp(1'b0));
  Seven_Seg_Hex seven_seg_hex_2 (.d(Address[7:4]), .dp(1'b0));
  LED led_1 (.in(clk));
  LED led_2 (.in(BRAM));
  LED led_3 (.in(RS));
  LED led_4 (.in(WS));
  LED led_5 (.in(Stack_Ovf));
  LED led_6 (.in(PC_Ovf));
  LED led_7 (.in(Int_E));
  LED led_8 (.in(Int_Ack));
  Seven_Seg_Hex seven_seg_hex_3 (.d(Address[3:0]), .dp(1'b0));
  Seven_Seg_Hex seven_seg_hex_4 (.d({3'b000, Instruction[4]}), .dp(1'b0));
  Seven_Seg_Hex seven_seg_hex_5 (.d(Instruction[3:0]), .dp(1'b0));
  Seven_Seg_Hex seven_seg_hex_6 (.d(register_1_q[7:4]), .dp(1'b0));
  Register #(.Bits(8)) register_1 (.D(PortID), .C(clk), .en(or_1_out), .Q(register_1_q));
  or or_1 (or_1_out, RS, WS);
  ROM #(.AddrBits(10), .isProgramMemory("true"), .Bits(18)) Program_Instructions (
    .A(Address), .sel(BRAM), .D(Program_Instructions_d));
  Button u_Int (.out(SendInt));
  Seven_Seg_Hex seven_seg_hex_7 (.d(register_1_q[3:0]), .dp(1'b0));
  Seven_Seg_Hex seven_seg_hex_8 (.d(register_2_q[7:4]), .dp(1'b0));
  Register #(.Bits(8)) register_2 (.D(Write), .C(clk), .en(WS), .Q(register_2_q));
  Seven_Seg_Hex seven_seg_hex_9 (.d(register_2_q[3:0]), .dp(1'b0));
  CPU cpu_1 (
    .Read(Read), .Int(Int), .clk(clk), .Instr(Program_Instructions_d), .Write(Write), .WS(WS), .RS(RS),
    .PortID(PortID), .Int_Ack(Int_Ack), .Int_E(Int_E), .PC_Ovf(PC_Ovf), .Stack_Ovf(Stack_Ovf),
    .Address(Address), .BRAM(BRAM));
  Seven_Seg_Hex seven_seg_hex_10 (.d(register_3_q[7:4]), .dp(1'b0));
  Register #(.Bits(8)) register_3 (.D(Read), .C(clk), .en(RS), .Q(register_3_q));
  Register #(.Bits(5)) register_4 (.D(Program_Instructions_d[4:0]), .C(clk), .en(BRAM), .Q(Instruction));
  Seven_Seg_Hex seven_seg_hex_11 (.d(register_3_q[3:0]), .dp(1'b0));
  Decoder #(.Selector_Bits(5)) decoder_1 (
    .sel(Instruction), .out_0(decoder_1_out_0), .out_1(decoder_1_out_1), .out_2(decoder_1_out_2),
    .out_3(decoder_1_out_3), .out_4(decoder_1_out_4), .out_5(decoder_1_out_5), .out_6(decoder_1_out_6),
    .out_7(decoder_1_out_7), .out_8(decoder_1_out_8), .out_9(decoder_1_out_9), .out_10(decoder_1_out_10),
    .out_11(decoder_1_out_11), .out_12(decoder_1_out_12), .out_13(decoder_1_out_13),
    .out_14(decoder_1_out_14), .out_15(decoder_1_out_15), .out_16(decoder_1_out_16),
    .out_17(decoder_1_out_17), .out_18(decoder_1_out_18), .out_19(decoder_1_out_19),
    .out_20(decoder_1_out_20), .out_21(decoder_1_out_21), .out_22(decoder_1_out_22),
    .out_23(decoder_1_out_23), .out_24(decoder_1_out_24), .out_25(decoder_1_out_25),
    .out_26(decoder_1_out_26), .out_27(decoder_1_out_27), .out_28(decoder_1_out_28),
    .out_29(decoder_1_out_29), .out_30(decoder_1_out_30), .out_31(decoder_1_out_31));
  LED led_9 (.in(decoder_1_out_1));
  LED led_10 (.in(decoder_1_out_3));
  LED led_11 (.in(decoder_1_out_5));
  LED led_12 (.in(decoder_1_out_7));
  LED led_13 (.in(decoder_1_out_9));
  LED led_14 (.in(decoder_1_out_11));
  LED led_15 (.in(decoder_1_out_13));
  LED led_16 (.in(decoder_1_out_15));
  LED led_17 (.in(decoder_1_out_17));
  LED led_18 (.in(decoder_1_out_19));
  LED led_19 (.in(decoder_1_out_21));
  LED led_20 (.in(decoder_1_out_23));
  LED led_21 (.in(decoder_1_out_25));
  LED led_22 (.in(decoder_1_out_27));
  LED led_23 (.in(decoder_1_out_29));
  LED led_24 (.in(decoder_1_out_31));
  LED led_25 (.in(decoder_1_out_0));
  LED led_26 (.in(decoder_1_out_2));
  LED led_27 (.in(decoder_1_out_4));
  LED led_28 (.in(decoder_1_out_6));
  LED led_29 (.in(decoder_1_out_8));
  LED led_30 (.in(decoder_1_out_10));
  LED led_31 (.in(decoder_1_out_12));
  LED led_32 (.in(decoder_1_out_14));
  LED led_33 (.in(decoder_1_out_16));
  LED led_34 (.in(decoder_1_out_18));
  LED led_35 (.in(decoder_1_out_20));
  LED led_36 (.in(decoder_1_out_22));
  LED led_37 (.in(decoder_1_out_24));
  LED led_38 (.in(decoder_1_out_26));
  LED led_39 (.in(decoder_1_out_28));
  LED led_40 (.in(decoder_1_out_30));
  not not_1 (not_1_out, SendInt);
  JK_FF jk_ff_1 (.J(Int), .C(clk), .K(Int_Ack), .nQ(jk_ff_1_nq));  // open: Q
  JK_FF jk_ff_2 (.J(not_1_out), .C(clk), .K(Int), .Q(jk_ff_2_q));  // open: nQ
  and and_1 (and_1_out, jk_ff_1_nq, SendInt, jk_ff_2_q);
  JK_FF jk_ff_3 (.J(and_1_out), .C(clk), .K(Int_Ack), .Q(Int));  // open: nQ

  // Notes on the sheet:
  //   clk: Hz: 2
  //   Instruction Address
  //   clk
  //   BRAM
  //   Read Strobe
  //   Write Strobe
  //   Program Stack Overflow
  //   Program Counter Overflow
  //   Interrupt Enabled
  //   Interrupt Acknolowedge
  //   Instruction
  //   Port ID
  //   contents of Program_Instructions (hex, n*v repeats v):
  //   3ff3e,3c,466,1076,618,217,19,0,61,460,3d,0,0,0,0,0,0,0,0,0,0,0,0,0,0,0,0,0,0,0,0,
  //   0,0,0,0,0,0,0,0,0,0,0,0,0,0,0,0,0,0,0,0,0,0,0,0,0,0,0,0,0,0,0,0,0,0,0,0,0,0,0,0,0,
  //   0,0,0,0,0,0,0,0,0,0,0,0,0,0,0,0,0,0,0,0,0,0,0,0,0,0,0,0,0,0,0,0,0,0,0,0,0,0,0,0,0,
  //   0,0,0,0,0,0,0,0,0,0,0,0,0,0,0,0,0,0,0,0,0,0,0,0,0,0,0,0,0,0,0,0,0,0,0,0,0,0,0,0,0,
  //   0,0,0,0,0,0,0,0,0,0,0,0,0,0,0,0,0,0,0,0,0,0,0,0,0,0,0,0,0,0,0,0,0,0,0,0,0,0,0,0,0,
  //   0,0,0,0,0,0,0,0,0,0,0,0,0,0,0,0,0,0,0,0,0,0,0,0,0,0,0,0,0,0,0,0,0,0,0,0,0,0,0,0,0,
  //   0,0,0,0,0,0,0,0,0,0,0,0,0,0,0,0,0,0,0,0,0,0,0,0,0,0,0,0,0,0,0,0,0,0,0,0,0,0,0,0,0,
  //   0,0,0,0,0,0,0,0,0,0,0,0,0,0,0,0,0,0,0,0,0,0,0,0,0,0,0,0,0,0,0,0,0,0,0,0,0,0,0,0,0,
  //   0,0,0,0,0,0,0,0,0,0,0,0,0,0,0,0,0,0,0,0,0,0,0,0,0,0,0,0,0,0,0,0,0,0,0,0,0,0,0,0,0,
  //   0,0,0,0,0,0,0,0,0,0,0,0,0,0,0,0,0,0,0,0,0,0,0,0,0,0,0,0,0,0,0,0,0,0,0,0,0,0,0,0,0,
  //   0,0,0,0,0,0,0,0,0,0,0,0,0,0,0,0,0,0,0,0,0,0,0,0,0,0,0,0,0,0,0,0,0,0,0,0,0,0,0,0,0,
  //   0,0,0,0,0,0,0,0,0,0,0,0,0,0,0,0,0,0,0,0,0,0,0,0,0,0,0,0,0,0,0,0,0,0,0,0,0,0,0,0,0,
  //   0,0,0,0,0,0,0,0,0,0,0,0,0,0,0,0,0,0,0,0,0,0,0,0,0,0,0,0,0,0,0,0,0,0,0,0,0,0,0,0,0,
  //   0,0,0,0,0,0,0,0,0,0,0,0,0,0,0,0,0,0,0,0,0,0,0,0,0,0,0,0,0,0,0,0,0,0,0,0,0,0,0,0,0,
  //   0,0,0,0,0,0,0,0,0,0,0,0,0,0,0,0,0,0,0,0,0,0,0,0,0,0,0,0,0,0,0,0,0,0,0,0,0,0,0,0,0,
  //   0,0,0,0,0,0,0,0,0,0,0,0,0,0,0,0,0,0,0,0,0,0,0,0,0,0,0,0,0,0,0,0,0,0,0,0,0,0,0,0,0,
  //   0,0,0,0,0,0,0,0,0,0,0,0,0,0,0,0,0,0,0,0,0,0,0,0,0,0,0,0,0,0,0,0,0,0,0,0,0,0,0,0,0,
  //   0,0,0,0,0,0,0,0,0,0,0,0,0,0,0,0,0,0,0,0,0,0,0,0,0,0,0,0,0,0,0,0,0,0,0,0,0,0,0,0,0,
  //   0,0,0,0,0,0,0,0,0,0,0,0,0,0,0,0,0,0,0,0,0,0,0,0,0,0,0,0,0,0,0,0,0,0,0,0,0,0,0,0,0,
  //   0,0,0,0,0,0,0,0,0,0,0,0,0,0,0,0,0,0,0,0,0,0,0,0,0,0,0,0,0,0,0,0,0,0,0,0,0,0,0,0,0,
  //   0,0,0,0,0,0,0,0,0,0,0,0,0,0,0,0,0,0,0,0,0,0,0,0,0,0,0,0,0,0,0,0,0,0,0,0,0,0,0,0,0,
  //   0,0,0,0,0,0,0,0,0,0,0,0,0,0,0,0,0,0,0,0,0,0,0,0,0,0,0,0,0,0,0,0,0,0,0,0,0,0,0,0,0,
  //   0,0,0,0,0,0,0,0,0,0,0,0,0,0,0,0,0,0,0,0,0,0,0,0,0,0,0,0,0,0,0,0,0,0,0,0,0,0,0,0,0,
  //   0,0,0,0,0,0,0,0,0,0,0,0,0,0,0,0,0,0,0,0,0,0,0,0,0,0,0,0,0,0,0,0,0,0,0,0,0,0,0,0,0,
  //   0,0,0,0,0,0,0,0,0,0,0,0,0,0,0,0,0,0,0,0,0,0,0,0,0,0,0,0,0,0,0,0,0,0,0,0,0,0,0,0,0,
  //   0,0,0,0,0,0,0,0,817
  //   Port Write
  //   Port Read
  //   LOAD
  //   OR
  //   TEST
  //   ADDCY
  //   SUBCY
  //   SR0
  //   SRX
  //   RR
  //   SL1
  //   SLA
  //   INPUT
  //   JUMP
  //   RETURN
  //   FETCH
  //   RETURNI
  //   HALT
  //   AND
  //   XOR
  //   ADD
  //   SUB
  //   COMPARE
  //   SR1
  //   SRA
  //   SL0
  //   SLX
  //   RL
  //   OUTPUT
  //   CALL
  //   STORE
  //   ENABLE INT
  //   ISRADDRESS
endmodule
