// Digital circuit OCID.dig as structural Verilog
module OCID (
  input  [15:0] instruction,
  input  rst,
  input  clk,
  output [2:0] operation,
  output [3:0] registerA,
  output [3:0] registerB,
  output [7:0] kk
);

  wire not_1_out, register_1_q;
  wire [7:4] demultiplexer_1_out_1;
  wire [15:3] register_2_q;

  Register register_1 (.D(not_1_out), .Q(register_1_q));  // open: C, en
  not not_1 (not_1_out, register_1_q);
  Register #(.Bits(16)) register_2 (
    .D(instruction), .en(not_1_out), .Q({register_2_q[15:8], registerA, register_2_q[3], operation}));  // open: C
  Multiplexer multiplexer_1 (.sel(register_1_q));  // open: in_0, in_1, out
  Demultiplexer #(.Bits(8)) demultiplexer_1 (
    .sel(register_2_q[3]), .in(register_2_q[15:8]), .out_0(kk), .out_1({demultiplexer_1_out_1, registerB}));
  // NotConnected on demultiplexer_1_out_1[4]
  // Pins of 1 and 3 bits meet at operation
  // Pins of 1 and 4 bits meet at registerA
  // Pins of 1 and 4 bits meet at registerB
  // Pins of 1 and 8 bits meet at kk
  // Pins of 1 and 4 bits meet at demultiplexer_1_out_1
endmodule
