// Digital circuit Processor.dig as structural Verilog
module Processor (
);

  RegisterFile #(.AddrBits(4), .Bits(8)) registerfile_1 ();  // open: Din, we, Rw, C, Ra, Rb, Da, Db
  RAMSinglePort ramsingleport_1 ();  // open: A, str, C, ld, D
endmodule
