// Digital circuit ALU.dig as structural Verilog
module ALU (
  input  [7:0] in_1,
  input  [7:0] in_2,
  input  [3:0] op,
  input  C_i,
  output [7:0] out,
  output Z,
  output C_o
);

  wire multiplexer_2_out, not_2_out, sel;
  wire [7:0] multiplexer_1_out, not_1_out;
  wire [8:0] add_1_out, and_1_out, or_1_p3, rl_1_p2, rr_1_p2, sla_1_p3, slx_1_p2, sra_1_p3, srx_1_p2,
       xor_1_p3;

  NOT not_1 (.in(in_2), .out(not_1_out));
  not not_2 (not_2_out, C_i);
  Multiplexer #(.Bits(8)) multiplexer_1 (.sel(sel), .in_0(in_2), .in_1(not_1_out), .out(multiplexer_1_out));
  Multiplexer multiplexer_2 (.sel(sel), .in_0(C_i), .in_1(not_2_out), .out(multiplexer_2_out));
  AND and_1 (.in_1(in_1), .in_2(in_2), .out(and_1_out));
  // OR or_1: pin names not known; wires that end beside it: in_1, in_2, or_1_p3
  // XOR xor_1: pin names not known; wires that end beside it: in_1, in_2, xor_1_p3
  ADD add_1 (.in_1(in_1), .in_2(multiplexer_1_out), .C_in(multiplexer_2_out), .out(add_1_out));
  // SRA sra_1: pin names not known; wires that end beside it: in_1, C_i, sra_1_p3
  // SRX srx_1: pin names not known; wires that end beside it: in_1, srx_1_p2
  // RR rr_1: pin names not known; wires that end beside it: in_1, rr_1_p2
  // SLA sla_1: pin names not known; wires that end beside it: in_1, C_i, sla_1_p3
  // SLX slx_1: pin names not known; wires that end beside it: in_1, slx_1_p2
  // RL rl_1: pin names not known; wires that end beside it: in_1, rl_1_p2
  Multiplexer #(.Selector_Bits(4), .Bits(10)) multiplexer_3 (
    .sel(op), .in_0({10{1'b0}}), .in_1({2'b00, in_2}), .in_2({1'b0, and_1_out}), .in_3({1'b0, or_1_p3}),
    .in_4({1'b0, xor_1_p3}), .in_5({1'b0, add_1_out}), .in_6({1'b1, add_1_out}), .in_7({1'b0, sra_1_p3}),
    .in_8({1'b0, srx_1_p2}), .in_9({1'b0, rr_1_p2}), .in_10({1'b0, sla_1_p3}), .in_11({1'b0, slx_1_p2}),
    .in_12({1'b0, rl_1_p2}), .in_13({10{1'b0}}), .in_14({10{1'b0}}), .in_15({10{1'b0}}), .out({sel, C_o, out}));
  and and_2 (Z, ~out[0], ~out[1], ~out[2], ~out[3], ~out[4], ~out[5], ~out[6], ~out[7]);  // And
endmodule
