// Digital circuit AND.dig as structural Verilog
module AND (
  input  [7:0] in_1,
  input  [7:0] in_2,
  output [8:0] out
);

  assign out[7:0] = in_1 & in_2;  // And and_1, 8 bits wide

  assign out[8] = 1'b0;
endmodule
