// Digital circuit NOT.dig as structural Verilog
module NOT (
  input  [7:0] in,
  output [7:0] out
);

  not not_1 (out[0], in[0]);
  not not_2 (out[1], in[1]);
  not not_3 (out[2], in[2]);
  not not_4 (out[3], in[3]);
  not not_5 (out[4], in[4]);
  not not_6 (out[5], in[5]);
  not not_7 (out[6], in[6]);
  not not_8 (out[7], in[7]);
endmodule
