// Digital circuit SRX.dig as structural Verilog
module SRX (
  input  [7:0] in,
  output [8:0] out
);

  // Pins of 8 and 9 bits meet at {in[0], {2{in[7]}}, in[6:1]}

  assign out = {in[0], {2{in[7]}}, in[6:1]};
endmodule
