// Digital circuit XOR.dig as structural Verilog
module XOR (
  input  [7:0] in_1,
  input  [7:0] in_2,
  output [8:0] out
);

  assign out[7:0] = in_1 ^ in_2;  // XOr xor_1, 8 bits wide
  // Pins of 1 and 8 bits meet at in_1
  // Pins of 1 and 8 bits meet at in_2
  // Pins of 1 and 9 bits meet at {1'b0, out[7:0]}

  assign out[8] = 1'b0;
endmodule
