// Digital circuit ByteFlip.dig as structural Verilog
module ByteFlip (
  input  [7:0] D_in,
  output [7:0] D_out
);

  // Pins of 1 and 8 bits meet at D_in
  // Pins of 1 and 8 bits meet at {D_in[0], D_in[1], D_in[2], D_in[3], D_in[4], D_in[5], D_in[6], D_in[7]}

  assign D_out = {D_in[0], D_in[1], D_in[2], D_in[3], D_in[4], D_in[5], D_in[6], D_in[7]};
endmodule
