// Digital circuit PCStack_Add1.dig as structural Verilog
module PCStack_Add1 (
  input  [4:0] in,
  output [4:0] out,
  output C
);

  wire and_1_out, and_2_out, and_3_out;

  not not_1 (out[0], in[0]);
  xor xor_1 (out[1], in[0], in[1]);
  and and_1 (and_1_out, in[0], in[1]);
  xor xor_2 (out[2], and_1_out, in[2]);
  and and_2 (and_2_out, and_1_out, in[2]);
  xor xor_3 (out[3], and_2_out, in[3]);
  and and_3 (and_3_out, and_2_out, in[3]);
  xor xor_4 (out[4], and_3_out, in[4]);
  and and_4 (C, and_3_out, in[4]);
endmodule
