// Digital circuit PC_Add1.dig as structural Verilog
module PC_Add1 (
  input  [9:0] in,
  output [9:0] out,
  output C
);

  wire and_1_out, and_2_out, and_3_out, and_4_out, and_5_out, and_6_out, and_7_out, and_8_out;

  not not_1 (out[0], in[0]);
  xor xor_1 (out[1], in[0], in[1]);
  and and_1 (and_1_out, in[0], in[1]);
  xor xor_2 (out[2], and_1_out, in[2]);
  and and_2 (and_2_out, and_1_out, in[2]);
  xor xor_3 (out[3], and_2_out, in[3]);
  and and_3 (and_3_out, and_2_out, in[3]);
  xor xor_4 (out[4], and_3_out, in[4]);
  and and_4 (and_4_out, and_3_out, in[4]);
  xor xor_5 (out[5], and_4_out, in[5]);
  and and_5 (and_5_out, and_4_out, in[5]);
  xor xor_6 (out[6], and_5_out, in[6]);
  and and_6 (and_6_out, and_5_out, in[6]);
  xor xor_7 (out[7], and_6_out, in[7]);
  and and_7 (and_7_out, and_6_out, in[7]);
  xor xor_8 (out[8], and_7_out, in[8]);
  and and_8 (and_8_out, and_7_out, in[8]);
  xor xor_9 (out[9], and_8_out, in[9]);
  and and_9 (C, and_8_out, in[9]);
endmodule
