// Digital circuit program24to18bits.dig as structural Verilog
module program24to18bits (
  input  [23:0] in,
  output [3:0] reg1,
  output [3:0] reg2,
  output [7:0] val,
  output [9:0] addr,
  output [4:0] Instruction,
  output sel,
  output [1:0] opt,
  output [17:0] out
);


  assign addr = {in[1:0], in[15:8]};
  assign Instruction = in[7:3];
  assign opt = in[23:22];
  assign out = {in[1:0], in[15:8], in[23:22], in[2], in[7:3]};
  assign reg1 = {in[9:8], in[23:22]};
  assign reg2 = in[13:10];
  assign sel = in[2];
  assign val = {in[1:0], in[15:10]};
endmodule
