// Digital circuit ADD.dig as structural Verilog
module ADD (
  input  [7:0] in_1,
  input  [7:0] in_2,
  input  C_in,
  output [8:0] out
);

  wire and_1_out, and_2_out, and_3_out, and_4_out, and_5_out, and_6_out, and_7_out, and_8_out, and_9_out,
       and_10_out, and_11_out, and_12_out, and_13_out, and_14_out, and_15_out, and_16_out, and_17_out,
       and_18_out, and_19_out, and_20_out, and_21_out, and_22_out, and_23_out, and_24_out, or_1_out,
       or_2_out, or_3_out, or_4_out, or_5_out, or_6_out, or_7_out;

  xor xor_1 (out[0], C_in, in_1[0], in_2[0]);
  and and_1 (and_1_out, C_in, in_2[0]);
  and and_2 (and_2_out, C_in, in_2[0]);
  and and_3 (and_3_out, in_1[0], in_2[0]);
  xor xor_2 (out[1], or_1_out, in_1[1], in_2[1]);
  and and_4 (and_4_out, or_1_out, in_1[1]);
  and and_5 (and_5_out, or_1_out, in_2[1]);
  and and_6 (and_6_out, in_1[1], in_2[1]);
  xor xor_3 (out[2], or_2_out, in_1[2], in_2[2]);
  and and_7 (and_7_out, or_2_out, in_1[2]);
  and and_8 (and_8_out, or_2_out, in_2[2]);
  and and_9 (and_9_out, in_1[2], in_2[2]);
  xor xor_4 (out[3], or_3_out, in_1[3], in_2[3]);
  and and_10 (and_10_out, or_3_out, in_1[3]);
  and and_11 (and_11_out, or_3_out, in_2[3]);
  and and_12 (and_12_out, in_1[3], in_2[3]);
  xor xor_5 (out[4], or_4_out, in_1[4], in_2[4]);
  and and_13 (and_13_out, or_4_out, in_1[4]);
  and and_14 (and_14_out, or_4_out, in_2[4]);
  and and_15 (and_15_out, in_1[4], in_2[4]);
  xor xor_6 (out[5], or_5_out, in_1[5], in_2[5]);
  and and_16 (and_16_out, or_5_out, in_1[5]);
  and and_17 (and_17_out, or_5_out, in_2[5]);
  and and_18 (and_18_out, in_1[5], in_2[5]);
  xor xor_7 (out[6], or_6_out, in_1[6], in_2[6]);
  and and_19 (and_19_out, or_6_out, in_1[6]);
  and and_20 (and_20_out, or_6_out, in_2[6]);
  and and_21 (and_21_out, in_1[6], in_2[6]);
  xor xor_8 (out[7], or_7_out, in_1[7], in_2[7]);
  and and_22 (and_22_out, or_7_out, in_1[7]);
  and and_23 (and_23_out, or_7_out, in_2[7]);
  and and_24 (and_24_out, in_1[7], in_2[7]);
  or or_1 (or_1_out, and_1_out, and_2_out, and_3_out);
  or or_2 (or_2_out, and_4_out, and_5_out, and_6_out);
  or or_3 (or_3_out, and_7_out, and_8_out, and_9_out);
  or or_4 (or_4_out, and_10_out, and_11_out, and_12_out);
  or or_5 (or_5_out, and_13_out, and_14_out, and_15_out);
  or or_6 (or_6_out, and_16_out, and_17_out, and_18_out);
  or or_7 (or_7_out, and_19_out, and_20_out, and_21_out);
  or or_8 (out[8], and_22_out, and_23_out, and_24_out);
  // Pins of 8 and 9 bits meet at out
endmodule
