// Digital circuit CPU.dig as structural Verilog
module CPU (
  input  [7:0] read,
  input  clk,
  input  Interrupt,
  output [7:0] write,
  output WriteStrobe,
  output ReadStrobe,
  output [7:0] PortID,
  output Interrupt_Ack
);

  wire alu_1_c_o, alu_1_z, and_1_out, and_2_out, and_3_out, and_4_out, and_5_out, and_6_out, and_7_out,
       and_10_out, and_11_out, and_12_out, C, ContrAddress, ContrFlag1, ContrFlag2, decoder_1_out_0,
       decoder_1_out_1, decoder_1_out_2, decoder_1_out_3, decoder_1_out_4, decoder_1_out_5, decoder_1_out_6,
       decoder_1_out_7, decoder_1_out_8, decoder_1_out_9, decoder_1_out_10, decoder_1_out_11,
       decoder_1_out_12, decoder_1_out_13, decoder_1_out_14, decoder_1_out_15, decoder_1_out_16,
       decoder_1_out_17, decoder_1_out_18, decoder_1_out_19, decoder_1_out_20, decoder_1_out_21,
       decoder_1_out_22, decoder_1_out_23, decoder_1_out_24, decoder_1_out_25, decoder_1_out_26,
       decoder_1_out_27, decoder_1_out_28, decoder_1_out_29, decoder_1_out_30, decoder_1_out_31, EW,
       InstrExecute, InstrFetch, InstrFlag1, InstrFlag2, Interrupt_t, InterruptEnabled, InterruptFlag,
       multiplexer_3_out, multiplexer_5_out, multiplexer_6_out, multiplexer_7_out, not_1_out, not_2_out,
       or_1_out, or_2_out, or_3_out, pc_add1_1_c, pcstack_1_c, ReadWrite, sel, UpdateFlags, Z;
  wire [1:0] and_8_out, Context_q;
  wire [3:0] op, register_1_q, register_1_q_2, register_2_q, register_2_q_2;
  wire [4:0] Instruction, multiplexer_2_out, Program_Instructions_d, StackCounter;
  wire [7:0] ALU_out, demultiplexer_2_out_0, demultiplexer_3_out_0, multiplexer_1_out, multiplexer_4_out,
       Reg1, Reg2;
  wire [9:0] Address, InstrAddress, ISRAddress, multiplexer_8_out, pc_add1_1_out, pcstack_1_out;
  wire [12:0] Program_Instructions_d_2;

  Seven_Seg_Hex seven_seg_hex_1 (.d({2'b00, Address[9:8]}), .dp(1'b0));
  Register #(.Bits(8)) register_1 (.D(PortID), .C(clk), .en(WriteStrobe), .Q({register_1_q_2, register_1_q}));
  Register #(.Bits(8)) register_2 (.D(write), .C(clk), .en(WriteStrobe), .Q({register_2_q_2, register_2_q}));
  Seven_Seg_Hex seven_seg_hex_2 (.d({2'b00, ISRAddress[9:8]}), .dp(1'b0));
  Seven_Seg_Hex seven_seg_hex_3 (.d(Address[7:4]), .dp(1'b0));
  Seven_Seg_Hex seven_seg_hex_4 (.d(register_1_q_2), .dp(1'b0));
  Seven_Seg_Hex seven_seg_hex_5 (.d(register_2_q_2), .dp(1'b0));
  Seven_Seg_Hex seven_seg_hex_6 (.d(ISRAddress[7:4]), .dp(1'b0));
  Seven_Seg_Hex seven_seg_hex_7 (.d(Address[3:0]), .dp(1'b0));
  Seven_Seg_Hex seven_seg_hex_8 (.d(register_1_q), .dp(1'b0));
  Seven_Seg_Hex seven_seg_hex_9 (.d(register_2_q), .dp(1'b0));
  Seven_Seg_Hex seven_seg_hex_10 (.d(ISRAddress[3:0]), .dp(1'b0));
  Seven_Seg_Hex seven_seg_hex_11 (.d({InstrAddress[1:0], InstrFlag2, InstrFlag1}), .dp(1'b0));
  Seven_Seg_Hex seven_seg_hex_12 (.d({2'b00, InstrAddress[9:8]}), .dp(1'b0));
  Seven_Seg_Hex seven_seg_hex_13 (.d({3'b000, StackCounter[4]}), .dp(1'b0));
  Seven_Seg_Hex seven_seg_hex_14 (.d({3'b000, Instruction[4]}), .dp(1'b0));
  Seven_Seg_Hex seven_seg_hex_15 (.d(InstrAddress[9:6]), .dp(1'b0));
  Seven_Seg_Hex seven_seg_hex_16 (.d(InstrAddress[7:4]), .dp(1'b0));
  ROM #(.AddrBits(10), .isProgramMemory("true"), .Bits(18)) Program_Instructions (
    .A(Address), .sel(InstrFetch), .D({Program_Instructions_d_2, Program_Instructions_d}));
  D_FF d_ff_1 (.D(InstrFetch), .C(clk), .Q(InstrExecute), .nQ(InstrFetch));
  Seven_Seg_Hex seven_seg_hex_17 (.d(StackCounter[3:0]), .dp(1'b0));
  Seven_Seg_Hex seven_seg_hex_18 (.d(Instruction[3:0]), .dp(1'b0));
  Seven_Seg_Hex seven_seg_hex_19 (.d(InstrAddress[5:2]), .dp(1'b0));
  Seven_Seg_Hex seven_seg_hex_20 (.d(InstrAddress[5:2]), .dp(1'b0));
  Seven_Seg_Hex seven_seg_hex_21 (.d(InstrAddress[3:0]), .dp(1'b0));
  Demultiplexer demultiplexer_1 (.sel(ContrFlag1), .in(ReadWrite), .out_0(ReadStrobe), .out_1(WriteStrobe));
  Multiplexer #(.Bits(8)) multiplexer_1 (.sel(ReadWrite), .in_0(ALU_out), .in_1(read), .out(multiplexer_1_out));
  Decoder #(.Selector_Bits(5)) decoder_1 (
    .sel(Instruction), .out_0(decoder_1_out_0), .out_1(decoder_1_out_1), .out_2(decoder_1_out_2),
    .out_3(decoder_1_out_3), .out_4(decoder_1_out_4), .out_5(decoder_1_out_5), .out_6(decoder_1_out_6),
    .out_7(decoder_1_out_7), .out_8(decoder_1_out_8), .out_9(decoder_1_out_9), .out_10(decoder_1_out_10),
    .out_11(decoder_1_out_11), .out_12(decoder_1_out_12), .out_13(decoder_1_out_13),
    .out_14(decoder_1_out_14), .out_15(decoder_1_out_15), .out_16(decoder_1_out_16),
    .out_17(decoder_1_out_17), .out_18(decoder_1_out_18), .out_19(decoder_1_out_19),
    .out_20(decoder_1_out_20), .out_21(decoder_1_out_21), .out_22(decoder_1_out_22),
    .out_23(decoder_1_out_23), .out_24(decoder_1_out_24), .out_25(decoder_1_out_25),
    .out_26(decoder_1_out_26), .out_27(decoder_1_out_27), .out_28(decoder_1_out_28),
    .out_29(decoder_1_out_29), .out_30(decoder_1_out_30), .out_31(decoder_1_out_31));
  LED led_1 (.in(InstrExecute));
  LED led_2 (.in(InstrFetch));
  Register #(.Bits(5)) InstructionReg (.D(Program_Instructions_d), .C(clk), .en(InstrFetch), .Q(Instruction));
  Register #(.Bits(13)) register_3 (
    .D(Program_Instructions_d_2), .C(clk), .en(InstrFetch), .Q({InstrAddress, InstrFlag2, InstrFlag1, sel}));
  LED led_3 (.in(decoder_1_out_1));
  LED led_4 (.in(decoder_1_out_3));
  LED led_5 (.in(decoder_1_out_5));
  LED led_6 (.in(decoder_1_out_7));
  LED led_7 (.in(decoder_1_out_9));
  LED led_8 (.in(decoder_1_out_11));
  LED led_9 (.in(decoder_1_out_13));
  LED led_10 (.in(decoder_1_out_15));
  LED led_11 (.in(decoder_1_out_17));
  LED led_12 (.in(decoder_1_out_19));
  LED led_13 (.in(decoder_1_out_21));
  LED led_14 (.in(decoder_1_out_23));
  LED led_15 (.in(decoder_1_out_25));
  LED led_16 (.in(decoder_1_out_27));
  LED led_17 (.in(decoder_1_out_29));
  LED led_18 (.in(decoder_1_out_31));
  LED led_19 (.in(sel));
  LED led_20 (.in(InstrFlag1));
  LED led_21 (.in(InstrFlag2));
  LED led_22 (.in(InterruptEnabled));
  LED led_23 (.in(Interrupt_t));
  LED led_24 (.in(Interrupt_Ack));
  RegisterBank registerbank_1 (
    .in(multiplexer_1_out), .A_1({InstrAddress[1:0], InstrFlag2, InstrFlag1}), .A_2(InstrAddress[5:2]),
    .EW(EW), .clk(clk), .out_1(Reg1), .out_2(Reg2));
  LED led_25 (.in(decoder_1_out_0));
  LED led_26 (.in(decoder_1_out_2));
  LED led_27 (.in(decoder_1_out_4));
  LED led_28 (.in(decoder_1_out_6));
  LED led_29 (.in(decoder_1_out_8));
  LED led_30 (.in(decoder_1_out_10));
  LED led_31 (.in(decoder_1_out_12));
  LED led_32 (.in(decoder_1_out_14));
  LED led_33 (.in(decoder_1_out_16));
  LED led_34 (.in(decoder_1_out_18));
  LED led_35 (.in(decoder_1_out_20));
  LED led_36 (.in(decoder_1_out_22));
  LED led_37 (.in(decoder_1_out_24));
  LED led_38 (.in(decoder_1_out_26));
  LED led_39 (.in(decoder_1_out_28));
  LED led_40 (.in(decoder_1_out_30));
  and and_1 (and_1_out, ReadWrite, ContrFlag1);
  Demultiplexer #(.Bits(8)) demultiplexer_2 (.sel(and_1_out), .in(Reg1), .out_0(demultiplexer_2_out_0), .out_1(write));
  and and_2 (and_2_out, InterruptFlag, ContrFlag1);
  or or_1 (or_1_out, Interrupt_t, and_2_out);
  and and_3 (and_3_out, sel, ~Interrupt_t);  // And
  Multiplexer #(.Bits(5)) multiplexer_2 (
    .sel(Interrupt_t), .in_0(Instruction), .in_1(5'b11000), .out(multiplexer_2_out));
  LED led_41 (.in(clk));
  not not_1 (not_1_out, Z);
  not not_2 (not_2_out, C);
  Multiplexer #(.Selector_Bits(2)) multiplexer_3 (
    .sel({InstrFlag2, InstrFlag1}), .in_0(Z), .in_1(C), .in_2(not_1_out), .in_3(not_2_out),
    .out(multiplexer_3_out));
  Register Enable_Interrupt (.D(and_3_out), .C(clk), .en(or_1_out), .Q(InterruptEnabled));
  // ProgramController programcontroller_1: pin names not known; wires that end beside it: multiplexer_2_out, InstrExecute, {InterruptFlag, ContrFlag2, ContrFlag1, ContrAddress, ReadWrite, EW, UpdateFlags, op}
  Multiplexer #(.Bits(8)) multiplexer_4 (.sel(sel), .in_0(Reg2), .in_1(InstrAddress[9:2]), .out(multiplexer_4_out));
  and and_4 (and_4_out, InterruptEnabled, Interrupt);
  or or_2 (or_2_out, ~sel, Interrupt_t, InterruptFlag, multiplexer_3_out);  // Or
  Demultiplexer #(.Bits(8)) demultiplexer_3 (
    .sel(ReadWrite), .in(multiplexer_4_out), .out_0(demultiplexer_3_out_0), .out_1(PortID));
  Register register_4 (.D(and_4_out), .C(clk), .en(InstrExecute), .Q(Interrupt_t));
  and and_5 (and_5_out, or_2_out, ContrAddress);
  Register #(.Bits(2)) Context (.D({C, Z}), .C(clk), .en(Interrupt_t), .Q(Context_q));
  and and_6 (and_6_out, Interrupt_t, Interrupt);
  and and_7 (and_7_out, ~ContrAddress, ~ContrFlag1, InterruptFlag);  // And
  Multiplexer multiplexer_5 (.sel(ContrFlag1), .in_0(C), .in_1(ContrFlag2), .out(multiplexer_5_out));
  ALU alu_1 (
    .in_1(demultiplexer_2_out_0), .in_2(demultiplexer_3_out_0), .op(op), .C_i(multiplexer_5_out),
    .out(ALU_out), .Z(alu_1_z), .C_o(alu_1_c_o));
  Register register_5 (.D(and_6_out), .C(clk), .en(InstrExecute), .Q(Interrupt_Ack));
  and and_8 (and_8_out[0], ~Interrupt_t, and_5_out);  // And
  and and_9 (and_8_out[1], ContrFlag2, and_5_out);
  and and_10 (and_10_out, InterruptFlag, ContrFlag1);
  Register #(.Bits(10)) ISR_Address (.D(InstrAddress), .C(clk), .en(and_7_out), .Q(ISRAddress));
  Multiplexer multiplexer_6 (.sel(and_10_out), .in_0(alu_1_z), .in_1(Context_q[0]), .out(multiplexer_6_out));
  Multiplexer multiplexer_7 (.sel(and_10_out), .in_0(alu_1_c_o), .in_1(Context_q[1]), .out(multiplexer_7_out));
  Multiplexer #(.Selector_Bits(2), .Bits(10)) multiplexer_8 (
    .sel(and_8_out), .in_0(pc_add1_1_out), .in_1(pcstack_1_out), .in_2(ISRAddress), .in_3(InstrAddress),
    .out(multiplexer_8_out));
  Register u_Z (.D(multiplexer_6_out), .C(clk), .en(UpdateFlags), .Q(Z));
  Register u_C (.D(multiplexer_7_out), .C(clk), .en(UpdateFlags), .Q(C));
  and and_11 (and_11_out, ~Interrupt_t, InstrFetch);  // And
  and and_12 (and_12_out, and_5_out, ContrFlag1);
  or or_3 (or_3_out, and_5_out, and_11_out);
  Register #(.Bits(10)) PC (.D(multiplexer_8_out), .C(clk), .en(or_3_out), .Q(Address));
  PC_Add1 pc_add1_1 (.in(Address), .out(pc_add1_1_out), .C(pc_add1_1_c));
  LED led_42 (.in(pc_add1_1_c));
  PCStack pcstack_1 (
    .in(Address), .sel(ContrFlag2), .EN(and_12_out), .clk(clk), .C(pcstack_1_c), .out(pcstack_1_out),
    .N(StackCounter));
  LED led_43 (.in(pcstack_1_c));

  // Other names for the same wires on the sheet: RegAddress1[3:0] = {InstrAddress[1:0], InstrFlag2, InstrFlag1};
  //   InstrConst[7:0] = InstrAddress[9:2]; RegAddress2[3:0] = InstrAddress[5:2]; InterruptAck = Interrupt_Ack

  // Notes on the sheet:
  //   clk: Hz: 50
  //   JUMP aaa 23
  //   JUMP Z, aaa 23
  //   JUMP NZ, aaa 23
  //   JUMP C, aaa 23
  //   JUMP NC, aaa 23
  //   CALL aaa 24
  //   CALL Z, aaa 24
  //   CALL NZ, aaa 24
  //   CALL C, aaa 24
  //   CALL NC, aaa 24
  //   RETURN 25
  //   RETURN Z 25
  //   RETURN NZ 25
  //   RETURN C 25
  //   RETURN NC 25
  //   ADD sX, kk 6
  //   ADDCY sX, kk 7
  //   SUB sX, kk 8
  //   SUBCY sX, kk 9
  //   COMPARE sX, kk 10
  //   ADD sX, sY 6
  //   ADDCY sX, sY 7
  //   SUB sX, sY 8
  //   SUBCY sX, sY 9
  //   COMPARE sX, sY 10
  //   RETURNI ENABLE 29
  //   RETURNI DISABLE 29
  //   ENABLE INTERRUPT 28
  //   DISABLE INTERRUPT 28
  //   LOAD sX, kk 1
  //   AND sX, kk 2
  //   OR sX, kk 3
  //   XOR sX, kk 4
  //   TEST sX, kk 5
  //   LOAD sX, sY 1
  //   AND sX, sY 2
  //   OR sX, sY 3
  //   XOR sX, sY 4
  //   TEST sX, sY 5
  //   STORE sX, ss 26
  //   STORE sX, (sY) 26
  //   FETCH sX, ss 27
  //   FETCH sX, (sY) 27
  //   SR0 sX 11
  //   SR1 sX 12
  //   SRX sX 13
  //   SRA sX 14
  //   RL sX 15
  //   SL0 sX 16
  //   SL1 sX 17
  //   SLX sX 18
  //   SLA sX 19
  //   RL sX 20
  //   INPUT sX, pp 21
  //   INPUT sX, (sY) 21
  //   OUTPUT sX, pp 22
  //   OUTPUT sX, (sY) 22
  //   ISRADDRESS aaa 30
  //   contents of Program_Instructions (hex, n*v repeats v):
  //   3ff3e,3c,466,1076,618,217,19,0,61,466,3d,0,0,0,0,0,0,0,0,0,0,0,0,0,0,0,0,0,0,0,0,
  //   0,0,0,0,0,0,0,0,0,0,0,0,0,0,0,0,0,0,0,0,0,0,0,0,0,0,0,0,0,0,0,0,0,0,0,0,0,0,0,0,0,
  //   0,0,0,0,0,0,0,0,0,0,0,0,0,0,0,0,0,0,0,0,0,0,0,0,0,0,0,0,0,0,0,0,0,0,0,0,0,0,0,0,0,
  //   0,0,0,0,0,0,0,0,0,0,0,0,0,0,0,0,0,0,0,0,0,0,0,0,0,0,0,0,0,0,0,0,0,0,0,0,0,0,0,0,0,
  //   0,0,0,0,0,0,0,0,0,0,0,0,0,0,0,0,0,0,0,0,0,0,0,0,0,0,0,0,0,0,0,0,0,0,0,0,0,0,0,0,0,
  //   0,0,0,0,0,0,0,0,0,0,0,0,0,0,0,0,0,0,0,0,0,0,0,0,0,0,0,0,0,0,0,0,0,0,0,0,0,0,0,0,0,
  //   0,0,0,0,0,0,0,0,0,0,0,0,0,0,0,0,0,0,0,0,0,0,0,0,0,0,0,0,0,0,0,0,0,0,0,0,0,0,0,0,0,
  //   0,0,0,0,0,0,0,0,0,0,0,0,0,0,0,0,0,0,0,0,0,0,0,0,0,0,0,0,0,0,0,0,0,0,0,0,0,0,0,0,0,
  //   0,0,0,0,0,0,0,0,0,0,0,0,0,0,0,0,0,0,0,0,0,0,0,0,0,0,0,0,0,0,0,0,0,0,0,0,0,0,0,0,0,
  //   0,0,0,0,0,0,0,0,0,0,0,0,0,0,0,0,0,0,0,0,0,0,0,0,0,0,0,0,0,0,0,0,0,0,0,0,0,0,0,0,0,
  //   0,0,0,0,0,0,0,0,0,0,0,0,0,0,0,0,0,0,0,0,0,0,0,0,0,0,0,0,0,0,0,0,0,0,0,0,0,0,0,0,0,
  //   0,0,0,0,0,0,0,0,0,0,0,0,0,0,0,0,0,0,0,0,0,0,0,0,0,0,0,0,0,0,0,0,0,0,0,0,0,0,0,0,0,
  //   0,0,0,0,0,0,0,0,0,0,0,0,0,0,0,0,0,0,0,0,0,0,0,0,0,0,0,0,0,0,0,0,0,0,0,0,0,0,0,0,0,
  //   0,0,0,0,0,0,0,0,0,0,0,0,0,0,0,0,0,0,0,0,0,0,0,0,0,0,0,0,0,0,0,0,0,0,0,0,0,0,0,0,0,
  //   0,0,0,0,0,0,0,0,0,0,0,0,0,0,0,0,0,0,0,0,0,0,0,0,0,0,0,0,0,0,0,0,0,0,0,0,0,0,0,0,0,
  //   0,0,0,0,0,0,0,0,0,0,0,0,0,0,0,0,0,0,0,0,0,0,0,0,0,0,0,0,0,0,0,0,0,0,0,0,0,0,0,0,0,
  //   0,0,0,0,0,0,0,0,0,0,0,0,0,0,0,0,0,0,0,0,0,0,0,0,0,0,0,0,0,0,0,0,0,0,0,0,0,0,0,0,0,
  //   0,0,0,0,0,0,0,0,0,0,0,0,0,0,0,0,0,0,0,0,0,0,0,0,0,0,0,0,0,0,0,0,0,0,0,0,0,0,0,0,0,
  //   0,0,0,0,0,0,0,0,0,0,0,0,0,0,0,0,0,0,0,0,0,0,0,0,0,0,0,0,0,0,0,0,0,0,0,0,0,0,0,0,0,
  //   0,0,0,0,0,0,0,0,0,0,0,0,0,0,0,0,0,0,0,0,0,0,0,0,0,0,0,0,0,0,0,0,0,0,0,0,0,0,0,0,0,
  //   0,0,0,0,0,0,0,0,0,0,0,0,0,0,0,0,0,0,0,0,0,0,0,0,0,0,0,0,0,0,0,0,0,0,0,0,0,0,0,0,0,
  //   0,0,0,0,0,0,0,0,0,0,0,0,0,0,0,0,0,0,0,0,0,0,0,0,0,0,0,0,0,0,0,0,0,0,0,0,0,0,0,0,0,
  //   0,0,0,0,0,0,0,0,0,0,0,0,0,0,0,0,0,0,0,0,0,0,0,0,0,0,0,0,0,0,0,0,0,0,0,0,0,0,0,0,0,
  //   0,0,0,0,0,0,0,0,0,0,0,0,0,0,0,0,0,0,0,0,0,0,0,0,0,0,0,0,0,0,0,0,0,0,0,0,0,0,0,0,0,
  //   0,0,0,0,0,0,0,0,0,0,0,0,0,0,0,0,0,0,0,0,0,0,0,0,0,0,0,0,0,0,0,0,0,0,0,0,0,0,0,0,0,
  //   0,0,0,0,0,0,0,0,817
  //   InstrExecute
  //   InstrFetch
  //   LOAD
  //   OR
  //   TEST
  //   ADDCY
  //   SUBCY
  //   SR0
  //   SRX
  //   RR
  //   SL1
  //   SLA
  //   INPUT
  //   JUMP
  //   RETURN
  //   FETCH
  //   RETURNI
  //   sel
  //   InstrFlag1
  //   InstrFlag2
  //   InterruptEnabled
  //   Interrupt
  //   InterruptAck
  //   HALT
  //   AND
  //   XOR
  //   ADD
  //   SUB
  //   COMPARE
  //   SR1
  //   SRA
  //   SL0
  //   SLX
  //   RL
  //   OUTPUT
  //   CALL
  //   STORE
  //   ENABLE INT
  //   ISRADDRESS
  //   clk
endmodule
