// Digital circuit PCStack_Sub1.dig as structural Verilog
module PCStack_Sub1 (
  input  [4:0] in,
  output [4:0] out,
  output C
);

  wire or_1_out, or_2_out, or_3_out;

  not not_1 (out[0], in[0]);
  xnor xnor_1 (out[1], in[0], in[1]);
  or or_1 (or_1_out, in[0], in[1]);
  xnor xnor_2 (out[2], or_1_out, in[2]);
  or or_2 (or_2_out, or_1_out, in[2]);
  xnor xnor_3 (out[3], or_2_out, in[3]);
  or or_3 (or_3_out, or_2_out, in[3]);
  xnor xnor_4 (out[4], or_3_out, in[4]);
  nor nor_1 (C, or_3_out, in[4]);
endmodule
