// Digital circuit 4_bits_signed_int_multiplier.dig as structural Verilog
module _4_bits_signed_int_multiplier (
  input  [3:0] D,
  input  EN,
  input  C,
  input  RST,
  output ovf,
  output [3:0] Q
);

  wire fsm_1_q_1, fsm_1_q_2, fsm_1_q_3, fsm_1_q_4, fsm_1_q_5, not_1_out;
  wire [3:0] add_1_s, and_1_out, multiplexer_1_out, neg_1_out, register_3_q, undriven, undriven_2;
  wire [4:0] and_2_out, and_3_out, bitextender_1_out;
  wire [4:4] add_1_c_o, register_3_q_2;

  FSM fsm_1 (
    .RST_s(RST), .C(C), .EN(EN), .Q_1(fsm_1_q_1), .Q_2(fsm_1_q_2), .Q_3(fsm_1_q_3), .Q_4(fsm_1_q_4),
    .Q_5(fsm_1_q_5));  // open: Q_6
  Register #(.Bits(4)) register_1 (.D(undriven_2), .C(C), .en(fsm_1_q_2));  // open: Q
  Neg #(.Bits(4)) neg_1 (.in(undriven), .out(neg_1_out));
  Multiplexer #(.Bits(4), .Selector_Bits(2)) multiplexer_1 (
    .in_3(undriven), .out(multiplexer_1_out));  // open: sel, in_0, in_1, in_2
  Register #(.Bits(4)) register_2 (.D(multiplexer_1_out), .C(C), .en(fsm_1_q_3));  // open: Q
  // And and_1 has open pins: In_1=open, In_2=open, out=and_1_out
  not not_1 (not_1_out, fsm_1_q_1);
  Add #(.Bits(4)) add_1 (.a(register_3_q), .b(and_1_out), .c_i(1'b0), .s(add_1_s), .c_o(add_1_c_o[4]));
  BitExtender #(.inputBits(1), .outputBits(5)) bitextender_1 (.in(not_1_out), .out(bitextender_1_out));
  assign and_2_out = {add_1_c_o[4], add_1_s} & bitextender_1_out;  // And and_2, 5 bits wide
  Register #(.Bits(5)) register_3 (.D(and_2_out), .C(C), .en(fsm_1_q_4), .Q({register_3_q_2[4], register_3_q}));
  assign and_3_out = {register_3_q_2[4], register_3_q} & bitextender_1_out;  // And and_3, 5 bits wide
  Register #(.Bits(5)) register_4 (.D(and_3_out), .C(C), .en(fsm_1_q_5), .Q({ovf, Q}));
endmodule
