// Digital circuit FSM.dig as structural Verilog
module FSM (
  input  RST_s,
  input  C,
  input  EN,
  output Q_1,
  output Q_2,
  output Q_3,
  output Q_4,
  output Q_5,
  output Q_6
);

  wire not_1_out;
  wire [2:0] and_1_out, bitextender_1_out, multiplexer_1_out, register_1_q;

  not not_1 (not_1_out, RST_s);
  BitExtender #(.inputBits(1), .outputBits(3)) bitextender_1 (.in(not_1_out), .out(bitextender_1_out));
  assign and_1_out = multiplexer_1_out & bitextender_1_out;  // And and_1, 3 bits wide
  Register #(.Bits(3)) register_1 (.D(and_1_out), .C(C), .en(EN), .Q(register_1_q));
  Multiplexer #(.Selector_Bits(3), .Bits(3)) multiplexer_1 (
    .sel(register_1_q), .in_0(3'b001), .in_1(3'b010), .in_2(3'b011), .in_3(3'b100), .in_4(3'b101),
    .in_5(3'b110), .in_6(3'b111), .in_7(3'b000), .out(multiplexer_1_out));
  Multiplexer #(.Selector_Bits(3)) multiplexer_2 (
    .sel(register_1_q), .in_0(1'b1), .in_1(1'b0), .in_2(1'b0), .in_3(1'b0), .in_4(1'b0), .in_5(1'b0),
    .in_6(1'b0), .in_7(1'b0), .out(Q_1));
  Multiplexer #(.Selector_Bits(3)) multiplexer_3 (
    .sel(register_1_q), .in_0(1'b1), .in_1(1'b1), .in_2(1'b0), .in_3(1'b0), .in_4(1'b0), .in_5(1'b0),
    .in_6(1'b0), .in_7(1'b0), .out(Q_2));
  Multiplexer #(.Selector_Bits(3)) multiplexer_4 (
    .sel(register_1_q), .in_0(1'b1), .in_1(1'b0), .in_2(1'b1), .in_3(1'b0), .in_4(1'b0), .in_5(1'b0),
    .in_6(1'b0), .in_7(1'b0), .out(Q_3));
  Multiplexer #(.Selector_Bits(3)) multiplexer_5 (
    .sel(register_1_q), .in_0(1'b1), .in_1(1'b0), .in_2(1'b0), .in_3(1'b1), .in_4(1'b1), .in_5(1'b1),
    .in_6(1'b1), .in_7(1'b0), .out(Q_4));
  Multiplexer #(.Selector_Bits(3)) multiplexer_6 (
    .sel(register_1_q), .in_0(1'b1), .in_1(1'b0), .in_2(1'b0), .in_3(1'b0), .in_4(1'b0), .in_5(1'b0),
    .in_6(1'b0), .in_7(1'b1), .out(Q_5));
  Multiplexer #(.Selector_Bits(3)) multiplexer_7 (
    .sel(register_1_q), .in_0(1'b0), .in_1(1'b0), .in_2(1'b0), .in_3(1'b1), .in_4(1'b1), .in_5(1'b1),
    .in_6(1'b0), .in_7(1'b0), .out(Q_6));
endmodule
