// Digital circuit 4_bits_unsigned_int_multiplier.dig as structural Verilog
module _4_bits_unsigned_int_multiplier (
  input  [3:0] D,
  input  EN,
  input  C,
  input  RST,
  output ovf,
  output [3:0] Q
);

  wire fsm_1_q_1, fsm_1_q_2, fsm_1_q_3, fsm_1_q_4, fsm_1_q_5, fsm_1_q_6, not_1_out, reg_2_shft_r_1_q;
  wire [3:0] add_1_s, and_1_out, bitextender_2_out, reg_1_shft_r_1_q, register_1_q;
  wire [4:0] and_2_out, and_3_out, bitextender_1_out;
  wire [4:4] add_1_c_o, register_1_q_2;

  FSM fsm_1 (
    .RST_s(RST), .C(C), .EN(EN), .Q_1(fsm_1_q_1), .Q_2(fsm_1_q_2), .Q_3(fsm_1_q_3), .Q_4(fsm_1_q_4),
    .Q_5(fsm_1_q_5), .Q_6(fsm_1_q_6));
  not not_1 (not_1_out, fsm_1_q_1);
  reg_1_shft_r reg_1_shft_r_1 (.D(D), .en(fsm_1_q_2), .C(C), .RST_s(fsm_1_q_1), .sft(fsm_1_q_6), .Q(reg_1_shft_r_1_q));
  reg_2_shft_r reg_2_shft_r_1 (.D(D), .en(fsm_1_q_3), .C(C), .RST_s(fsm_1_q_1), .sft(fsm_1_q_6), .Q(reg_2_shft_r_1_q));
  BitExtender #(.inputBits(1), .outputBits(5)) bitextender_1 (.in(not_1_out), .out(bitextender_1_out));
  BitExtender #(.inputBits(1), .outputBits(4)) bitextender_2 (.in(reg_2_shft_r_1_q), .out(bitextender_2_out));
  assign and_1_out = reg_1_shft_r_1_q & bitextender_2_out;  // And and_1, 4 bits wide
  Add #(.Bits(4)) add_1 (.a(register_1_q), .b(and_1_out), .c_i(1'b0), .s(add_1_s), .c_o(add_1_c_o[4]));
  assign and_2_out = {add_1_c_o[4], add_1_s} & bitextender_1_out;  // And and_2, 5 bits wide
  Register #(.Bits(5)) register_1 (.D(and_2_out), .C(C), .en(fsm_1_q_4), .Q({register_1_q_2[4], register_1_q}));
  assign and_3_out = {register_1_q_2[4], register_1_q} & bitextender_1_out;  // And and_3, 5 bits wide
  Register #(.Bits(5)) register_2 (.D(and_3_out), .C(C), .en(fsm_1_q_5), .Q({ovf, Q}));
endmodule
