// Digital circuit reg_1_shft_r.dig as structural Verilog
module reg_1_shft_r (
  input  [3:0] D,
  input  en,
  input  C,
  input  RST_s,
  input  sft,
  output [3:0] Q
);

  wire multiplexer_1_out, multiplexer_2_out, multiplexer_3_out, multiplexer_4_out;

  Multiplexer #(.Selector_Bits(3)) multiplexer_1 (
    .sel({RST_s, sft, en}), .in_0(Q[0]), .in_1(D[0]), .in_2(1'b0), .in_3(1'b0), .in_4(1'b0), .in_5(1'b0),
    .in_6(1'b0), .in_7(1'b0), .out(multiplexer_1_out));
  D_FF d_ff_1 (.D(multiplexer_1_out), .C(C), .Q(Q[0]));  // open: nQ
  Multiplexer #(.Selector_Bits(3)) multiplexer_2 (
    .sel({RST_s, sft, en}), .in_0(Q[1]), .in_1(D[1]), .in_2(Q[0]), .in_3(Q[0]), .in_4(1'b0), .in_5(1'b0),
    .in_6(1'b0), .in_7(1'b0), .out(multiplexer_2_out));
  D_FF d_ff_2 (.D(multiplexer_2_out), .C(C), .Q(Q[1]));  // open: nQ
  Multiplexer #(.Selector_Bits(3)) multiplexer_3 (
    .sel({RST_s, sft, en}), .in_0(Q[2]), .in_1(D[2]), .in_2(Q[1]), .in_3(Q[1]), .in_4(1'b0), .in_5(1'b0),
    .in_6(1'b0), .in_7(1'b0), .out(multiplexer_3_out));
  D_FF d_ff_3 (.D(multiplexer_3_out), .C(C), .Q(Q[2]));  // open: nQ
  Multiplexer #(.Selector_Bits(3)) multiplexer_4 (
    .sel({RST_s, sft, en}), .in_0(Q[3]), .in_1(D[3]), .in_2(Q[2]), .in_3(Q[2]), .in_4(1'b0), .in_5(1'b0),
    .in_6(1'b0), .in_7(1'b0), .out(multiplexer_4_out));
  D_FF d_ff_4 (.D(multiplexer_4_out), .C(C), .Q(Q[3]));  // open: nQ
endmodule
